// Logisim project Atividade2.circ as structural Verilog
module FF (
  input  Set,
  input  CLK,
  input  Reset,
  output Q,
  output Ql
);

  wire nand_1_out, nand_2_out;

  nand nand_1 (nand_1_out, Set, CLK);
  nand nand_2 (nand_2_out, CLK, Reset);
  nand nand_3 (Q, nand_1_out, Ql);
  nand nand_4 (Ql, Q, nand_2_out);

  // Notes on the sheet:
  //   Flip-Flop Reset Set c/ Clock
endmodule

module FF_JK (
  input  J,
  input  CLK,
  input  K,
  output Q,
  output Ql
);

  wire nand_1_out, nand_2_out;

  nand nand_1 (nand_1_out, J, CLK, Ql);
  nand nand_2 (nand_2_out, Q, CLK, K);
  nand nand_3 (Q, nand_1_out, Ql);
  nand nand_4 (Ql, Q, nand_2_out);

  // Notes on the sheet:
  //   Flip-Flop JK
endmodule

module FF_JK_PC (
  input  PRESET,
  input  J,
  input  CLK,
  input  K,
  input  CLEAR,
  output Q,
  output Ql
);

  wire nand_1_out, nand_2_out, not_1_out, not_2_out;

  nand nand_1 (nand_1_out, J, CLK, Ql);
  nand nand_2 (nand_2_out, Q, CLK, K);
  not not_1 (not_1_out, PRESET);
  not not_2 (not_2_out, CLEAR);
  nand nand_3 (Q, not_1_out, nand_1_out, Ql);
  nand nand_4 (Ql, Q, nand_2_out, not_2_out);

  // Notes on the sheet:
  //   Flip-Flop JK com Entrada Preset e Clear
endmodule

module FF_JK_ME_PC (
  input  PRESET,
  input  J,
  input  CLK,
  input  K,
  input  CLEAR,
  output Q,
  output Qq
);

  wire nand_1_out, nand_2_out, nand_3_out, nand_4_out, nand_5_out, nand_6_out, not_1_out, not_2_out,
       not_3_out;

  nand nand_1 (nand_1_out, J, CLK, Qq);
  nand nand_2 (nand_2_out, Q, CLK, K);
  not not_1 (not_1_out, PRESET);
  not not_2 (not_2_out, CLEAR);
  nand nand_3 (nand_3_out, not_1_out, nand_1_out, nand_4_out);
  nand nand_4 (nand_4_out, nand_3_out, nand_2_out, not_2_out);
  not not_3 (not_3_out, CLK);
  nand nand_5 (nand_5_out, nand_3_out, not_3_out);
  nand nand_6 (nand_6_out, not_3_out, nand_4_out);
  nand nand_7 (Q, not_1_out, nand_5_out, Qq);
  nand nand_8 (Qq, Q, nand_6_out, not_2_out);

  // Notes on the sheet:
  //   Flip-Flop JK Mestre-Escravo com Entrada Preset e Clear
endmodule

module FF_JK_ME_PC_T (
  input  PRESET,
  input  J,
  input  CLK,
  input  CLEAR,
  output Q,
  output Qq
);

  wire nand_1_out, nand_2_out, nand_3_out, nand_4_out, nand_5_out, nand_6_out, not_1_out, not_2_out,
       not_3_out;

  nand nand_1 (nand_1_out, J, CLK, Qq);
  nand nand_2 (nand_2_out, Q, CLK, J);
  not not_1 (not_1_out, PRESET);
  not not_2 (not_2_out, CLEAR);
  nand nand_3 (nand_3_out, not_1_out, nand_1_out, nand_4_out);
  nand nand_4 (nand_4_out, nand_3_out, nand_2_out, not_2_out);
  not not_3 (not_3_out, CLK);
  nand nand_5 (nand_5_out, nand_3_out, not_3_out);
  nand nand_6 (nand_6_out, not_3_out, nand_4_out);
  nand nand_7 (Q, not_1_out, nand_5_out, Qq);
  nand nand_8 (Qq, Q, nand_6_out, not_2_out);

  // Notes on the sheet:
  //   Flip-Flop JK Mestre-Escravo com Entrada Preset e Clear T
endmodule

module FF_JK_ME_PC_D (
  input  PRESET,
  input  J,
  input  CLK,
  input  CLEAR,
  output Q,
  output Qq
);

  wire nand_1_out, nand_2_out, nand_3_out, nand_4_out, nand_5_out, nand_6_out, not_1_out, not_2_out,
       not_3_out, not_4_out;

  not not_1 (not_1_out, J);
  nand nand_1 (nand_1_out, J, CLK, Qq);
  nand nand_2 (nand_2_out, Q, CLK, not_1_out);
  not not_2 (not_2_out, PRESET);
  not not_3 (not_3_out, CLEAR);
  nand nand_3 (nand_3_out, not_2_out, nand_1_out, nand_4_out);
  nand nand_4 (nand_4_out, nand_3_out, nand_2_out, not_3_out);
  not not_4 (not_4_out, CLK);
  nand nand_5 (nand_5_out, nand_3_out, not_4_out);
  nand nand_6 (nand_6_out, not_4_out, nand_4_out);
  nand nand_7 (Q, not_2_out, nand_5_out, Qq);
  nand nand_8 (Qq, Q, nand_6_out, not_3_out);

  // Notes on the sheet:
  //   Flip-Flop JK Mestre-Escravo com Entrada Preset e Clear T
endmodule

module DivisorDeFrenquencia (
  input  J,
  output out_2,
  output out_3,
  output out_4,
  output out_5
);

  wire CLEAR_out, CLK_out, ff_jk_me_pc_t_1_qq, ff_jk_me_pc_t_2_qq, ff_jk_me_pc_t_3_qq, ff_jk_me_pc_t_4_qq,
       not_1_out, not_2_out, not_3_out, not_4_out, not_5_out, not_6_out, not_7_out, not_8_out, not_9_out,
       not_10_out, not_11_out, not_12_out, not_13_out, not_14_out, not_15_out, not_16_out, not_17_out,
       not_18_out, not_19_out, not_20_out, PRESET_out;
  wire [6:0] decodificador_hex_1_out_2;

  not not_1 (not_1_out, J);
  not not_2 (not_2_out, J);
  _7_Segment_Display u_7_segment_display_1 (
    .f(not_1_out), .a(not_2_out), .b(1'b1), .e(not_3_out), .d(not_4_out), .c(1'b1));  // open: g, dp
  not not_3 (not_3_out, J);
  not not_4 (not_4_out, J);
  Button PRESET (.out(PRESET_out));
  Button CLEAR (.out(CLEAR_out));
  Clock CLK (.out(CLK_out));
  not not_5 (not_5_out, out_5);
  not not_6 (not_6_out, out_5);
  _7_Segment_Display u_7_segment_display_2 (
    .f(not_5_out), .a(not_6_out), .b(1'b1), .e(not_7_out), .d(not_8_out), .c(1'b1));  // open: g, dp
  not not_7 (not_7_out, out_5);
  not not_8 (not_8_out, out_5);
  not not_9 (not_9_out, out_4);
  not not_10 (not_10_out, out_4);
  not not_11 (not_11_out, out_3);
  _7_Segment_Display u_7_segment_display_3 (
    .f(not_9_out), .a(not_10_out), .b(1'b1), .e(not_12_out), .d(not_13_out), .c(1'b1));  // open: g, dp
  _7_Segment_Display u_7_segment_display_4 (
    .f(not_11_out), .a(not_16_out), .b(1'b1), .e(not_14_out), .d(not_15_out), .c(1'b1));  // open: g, dp
  not not_12 (not_12_out, out_4);
  not not_13 (not_13_out, out_4);
  not not_14 (not_14_out, out_3);
  not not_15 (not_15_out, out_3);
  not not_16 (not_16_out, out_3);
  not not_17 (not_17_out, out_2);
  not not_18 (not_18_out, out_2);
  _7_Segment_Display u_7_segment_display_5 (
    .f(not_17_out), .a(not_18_out), .b(1'b1), .e(not_19_out), .d(not_20_out), .c(1'b1));  // open: g, dp
  not not_19 (not_19_out, out_2);
  not not_20 (not_20_out, out_2);
  FF_JK_ME_PC_T ff_jk_me_pc_t_1 (
    .PRESET(PRESET_out), .J(J), .CLK(CLK_out), .CLEAR(CLEAR_out), .Q(out_2), .Qq(ff_jk_me_pc_t_1_qq));
  // NoConnect on ff_jk_me_pc_t_1_qq
  decodificador_hex decodificador_hex_1 (.in_1({out_5, out_4, out_3, out_2}), .out_2(decodificador_hex_1_out_2));
  _7_Segment_Display u_7_segment_display_6 (
    .g(decodificador_hex_1_out_2[6]), .f(decodificador_hex_1_out_2[5]), .a(decodificador_hex_1_out_2[0]),
    .b(decodificador_hex_1_out_2[1]), .e(decodificador_hex_1_out_2[4]), .d(decodificador_hex_1_out_2[3]),
    .c(decodificador_hex_1_out_2[2]));  // open: dp
  FF_JK_ME_PC_T ff_jk_me_pc_t_2 (
    .PRESET(PRESET_out), .J(J), .CLK(out_2), .CLEAR(CLEAR_out), .Q(out_3), .Qq(ff_jk_me_pc_t_2_qq));
  // NoConnect on ff_jk_me_pc_t_2_qq
  FF_JK_ME_PC_T ff_jk_me_pc_t_3 (
    .PRESET(PRESET_out), .J(J), .CLK(out_3), .CLEAR(CLEAR_out), .Q(out_4), .Qq(ff_jk_me_pc_t_3_qq));
  // NoConnect on ff_jk_me_pc_t_3_qq
  FF_JK_ME_PC_T ff_jk_me_pc_t_4 (
    .PRESET(PRESET_out), .J(J), .CLK(out_4), .CLEAR(CLEAR_out), .Q(out_5), .Qq(ff_jk_me_pc_t_4_qq));
  // NoConnect on ff_jk_me_pc_t_4_qq

  // Other names for the same wires on the sheet: B = J; S[3:0] = {out_5, out_4, out_3, out_2}

  // Notes on the sheet:
  //   ENTRADA
  //   Divisor de Frequência com FF_JK_ME_PC_T
  //   SAIDA PARALELA
  //   SAÍDA
endmodule

module RegistradorDeDeslocamento (
  input  [3:0] E_PARALELA,
  input  E_SERIAL,
  output S_SERIAL,
  output out_4,
  output out_5,
  output out_6,
  output out_7,
  output [3:0] S_PARALELA
);

  wire CLEAR_out, CLK_out, delay_1_clear, delay_1_preset, delay_2_clear, delay_2_preset, delay_3_clear,
       delay_3_preset, delay_4_clear, delay_4_preset, ENABLE_out, ff_jk_me_pc_d_1_qq, ff_jk_me_pc_d_2_qq,
       ff_jk_me_pc_d_3_qq, ff_jk_me_pc_d_4_qq, not_1_out, not_2_out, not_3_out, not_4_out, not_5_out,
       not_6_out, not_7_out, not_8_out, not_9_out, not_10_out, not_11_out, not_12_out, not_13_out,
       not_14_out, not_15_out, not_16_out, not_17_out, not_18_out, not_19_out, not_20_out, not_21_out,
       not_22_out, not_23_out, not_24_out, not_25_out, not_26_out, not_27_out, not_28_out, not_29_out,
       not_30_out, not_31_out, not_32_out, not_33_out, not_34_out, not_35_out, not_36_out, not_37_out,
       not_38_out, not_39_out, not_40_out, or_1_out, or_2_out, or_3_out, or_4_out;

  not not_1 (not_1_out, E_PARALELA[3]);
  not not_2 (not_2_out, E_PARALELA[2]);
  not not_3 (not_3_out, E_PARALELA[2]);
  not not_4 (not_4_out, E_PARALELA[3]);
  _7_Segment_Display u_7_segment_display_1 (
    .f(not_2_out), .a(not_3_out), .b(1'b1), .e(not_5_out), .d(not_6_out), .c(1'b1));  // open: g, dp
  _7_Segment_Display u_7_segment_display_2 (
    .f(not_4_out), .a(not_1_out), .b(1'b1), .e(not_7_out), .d(not_8_out), .c(1'b1));  // open: g, dp
  not not_5 (not_5_out, E_PARALELA[2]);
  not not_6 (not_6_out, E_PARALELA[2]);
  not not_7 (not_7_out, E_PARALELA[3]);
  not not_8 (not_8_out, E_PARALELA[3]);
  Button ENABLE (.out(ENABLE_out));
  Button CLEAR (.out(CLEAR_out));
  Clock CLK (.out(CLK_out));
  not not_9 (not_9_out, E_PARALELA[1]);
  not not_10 (not_10_out, E_PARALELA[1]);
  _7_Segment_Display u_7_segment_display_3 (
    .f(not_9_out), .a(not_10_out), .b(1'b1), .e(not_11_out), .d(not_12_out), .c(1'b1));  // open: g, dp
  _7_Segment_Display u_7_segment_display_4 (
    .f(not_14_out), .a(not_15_out), .b(1'b1), .e(not_13_out), .d(not_16_out), .c(1'b1));  // open: g, dp
  not not_11 (not_11_out, E_PARALELA[1]);
  not not_12 (not_12_out, E_PARALELA[1]);
  not not_13 (not_13_out, E_PARALELA[0]);
  not not_14 (not_14_out, E_PARALELA[0]);
  not not_15 (not_15_out, E_PARALELA[0]);
  not not_16 (not_16_out, E_PARALELA[0]);
  Delay delay_1 (.VALOR_PRESETADO(E_PARALELA[3]), .ENABLE(ENABLE_out), .PRESET(delay_1_preset), .CLEAR(delay_1_clear));
  or or_1 (or_1_out, delay_1_clear, CLEAR_out);
  not not_17 (not_17_out, E_SERIAL);
  not not_18 (not_18_out, E_SERIAL);
  _7_Segment_Display u_7_segment_display_5 (
    .f(not_17_out), .a(not_18_out), .b(1'b1), .e(not_19_out), .d(not_20_out), .c(1'b1));  // open: g, dp
  not not_19 (not_19_out, E_SERIAL);
  not not_20 (not_20_out, E_SERIAL);
  not not_21 (not_21_out, out_4);
  not not_22 (not_22_out, out_4);
  _7_Segment_Display u_7_segment_display_6 (
    .f(not_21_out), .a(not_22_out), .b(1'b1), .e(not_23_out), .d(not_24_out), .c(1'b1));  // open: g, dp
  not not_23 (not_23_out, out_4);
  not not_24 (not_24_out, out_4);
  FF_JK_ME_PC_D ff_jk_me_pc_d_1 (
    .PRESET(delay_1_preset), .J(E_SERIAL), .CLK(CLK_out), .CLEAR(or_1_out), .Q(out_4), .Qq(ff_jk_me_pc_d_1_qq));
  // NoConnect on ff_jk_me_pc_d_1_qq
  or or_2 (or_2_out, delay_2_clear, CLEAR_out);
  not not_25 (not_25_out, out_5);
  not not_26 (not_26_out, out_5);
  not not_27 (not_27_out, out_6);
  not not_28 (not_28_out, out_6);
  _7_Segment_Display u_7_segment_display_7 (
    .f(not_25_out), .a(not_26_out), .b(1'b1), .e(not_29_out), .d(not_30_out), .c(1'b1));  // open: g, dp
  _7_Segment_Display u_7_segment_display_8 (
    .f(not_27_out), .a(not_28_out), .b(1'b1), .e(not_31_out), .d(not_32_out), .c(1'b1));  // open: g, dp
  not not_29 (not_29_out, out_5);
  not not_30 (not_30_out, out_5);
  not not_31 (not_31_out, out_6);
  not not_32 (not_32_out, out_6);
  Delay delay_2 (.VALOR_PRESETADO(E_PARALELA[2]), .ENABLE(ENABLE_out), .PRESET(delay_2_preset), .CLEAR(delay_2_clear));
  not not_33 (not_33_out, out_7);
  not not_34 (not_34_out, out_7);
  _7_Segment_Display u_7_segment_display_9 (
    .f(not_33_out), .a(not_34_out), .b(1'b1), .e(not_35_out), .d(not_36_out), .c(1'b1));  // open: g, dp
  not not_35 (not_35_out, out_7);
  not not_36 (not_36_out, out_7);
  not not_37 (not_37_out, out_7);
  not not_38 (not_38_out, out_7);
  _7_Segment_Display u_7_segment_display_10 (
    .f(not_37_out), .a(not_38_out), .b(1'b1), .e(not_39_out), .d(not_40_out), .c(1'b1));  // open: g, dp
  not not_39 (not_39_out, out_7);
  not not_40 (not_40_out, out_7);
  FF_JK_ME_PC_D ff_jk_me_pc_d_2 (
    .PRESET(delay_2_preset), .J(out_4), .CLK(CLK_out), .CLEAR(or_2_out), .Q(out_5), .Qq(ff_jk_me_pc_d_2_qq));
  // NoConnect on ff_jk_me_pc_d_2_qq
  Delay delay_3 (.VALOR_PRESETADO(E_PARALELA[1]), .ENABLE(ENABLE_out), .PRESET(delay_3_preset), .CLEAR(delay_3_clear));
  or or_3 (or_3_out, delay_3_clear, CLEAR_out);
  FF_JK_ME_PC_D ff_jk_me_pc_d_3 (
    .PRESET(delay_3_preset), .J(out_5), .CLK(CLK_out), .CLEAR(or_3_out), .Q(out_6), .Qq(ff_jk_me_pc_d_3_qq));
  // NoConnect on ff_jk_me_pc_d_3_qq
  or or_4 (or_4_out, delay_4_clear, CLEAR_out);
  Delay delay_4 (.VALOR_PRESETADO(E_PARALELA[0]), .ENABLE(ENABLE_out), .PRESET(delay_4_preset), .CLEAR(delay_4_clear));
  FF_JK_ME_PC_D ff_jk_me_pc_d_4 (
    .PRESET(delay_4_preset), .J(out_6), .CLK(CLK_out), .CLEAR(or_4_out), .Q(out_7), .Qq(ff_jk_me_pc_d_4_qq));
  // NoConnect on ff_jk_me_pc_d_4_qq

  assign S_PARALELA = {out_4, out_5, out_6, out_7};
  assign S_SERIAL = out_7;

  // Other names for the same wires on the sheet: A[3:0] = E_PARALELA; B = E_SERIAL; C = out_7;
  //   S[3:0] = {out_4, out_5, out_6, out_7}

  // Notes on the sheet:
  //   Registrador de Deslocamento com FF_JK_ME_PC_D
  //   ENTRADA PARALELA
  //   ENTRADA SERIAL
  //   SAIDA PARALELA
  //   SAIDA SERIAL
endmodule

module RegistradorDeDeslocamentoUniversal (
  input  [1:0] SEL,
  input  [3:0] E_PARALELA,
  input  E_SERIAL_DIR,
  input  E_SERIAL_ESQ,
  output S_SERIAL,
  output [3:0] S_PARALELA
);

  wire CLEAR_out, CLK_out, ff_jk_me_pc_d_1_qq, ff_jk_me_pc_d_2_qq, ff_jk_me_pc_d_3_qq, ff_jk_me_pc_d_4_qq,
       mux_1_out_7, mux_2_out_7, mux_3_out_7, mux_4_out_7, not_1_out, not_2_out, not_3_out, not_4_out,
       not_5_out, not_6_out, not_7_out, not_8_out, not_9_out, not_10_out, not_11_out, not_12_out, not_13_out,
       not_14_out, not_15_out, not_16_out, not_17_out, not_18_out, not_19_out, not_20_out, not_21_out,
       not_22_out, not_23_out, not_24_out, not_25_out, not_26_out, not_27_out, not_28_out, not_29_out,
       not_30_out, not_31_out, not_32_out, not_33_out, not_34_out, not_35_out, not_36_out, not_37_out,
       not_38_out, not_39_out, not_40_out, not_41_out, not_42_out, not_43_out, not_44_out, not_45_out,
       not_46_out, not_47_out, not_48_out, not_49_out, not_50_out, not_51_out, not_52_out, PRESET_out;

  Button PRESET (.out(PRESET_out));
  Button CLEAR (.out(CLEAR_out));
  Clock CLK (.out(CLK_out));
  not not_1 (not_1_out, SEL[1]);
  not not_2 (not_2_out, SEL[1]);
  _7_Segment_Display u_7_segment_display_1 (
    .f(not_1_out), .a(not_2_out), .b(1'b1), .e(not_3_out), .d(not_4_out), .c(1'b1));  // open: g, dp
  not not_3 (not_3_out, SEL[1]);
  not not_4 (not_4_out, SEL[1]);
  not not_5 (not_5_out, SEL[0]);
  not not_6 (not_6_out, SEL[0]);
  _7_Segment_Display u_7_segment_display_2 (
    .f(not_5_out), .a(not_6_out), .b(1'b1), .e(not_7_out), .d(not_8_out), .c(1'b1));  // open: g, dp
  not not_7 (not_7_out, SEL[0]);
  not not_8 (not_8_out, SEL[0]);
  _7_Segment_Display u_7_segment_display_3 (
    .f(not_10_out), .a(not_11_out), .b(1'b1), .e(not_9_out), .d(not_14_out), .c(1'b1));  // open: g, dp
  not not_9 (not_9_out, E_PARALELA[3]);
  MUX mux_1 (
    .I0(S_PARALELA[3]), .I1(S_PARALELA[2]), .I2(E_SERIAL_ESQ), .I3(E_PARALELA[3]), .A(SEL[0]), .B(SEL[1]),
    .out_7(mux_1_out_7));
  not not_10 (not_10_out, E_PARALELA[3]);
  not not_11 (not_11_out, E_PARALELA[3]);
  not not_12 (not_12_out, E_PARALELA[2]);
  not not_13 (not_13_out, E_PARALELA[2]);
  _7_Segment_Display u_7_segment_display_4 (
    .f(not_12_out), .a(not_13_out), .b(1'b1), .e(not_15_out), .d(not_16_out), .c(1'b1));  // open: g, dp
  not not_14 (not_14_out, E_PARALELA[3]);
  not not_15 (not_15_out, E_PARALELA[2]);
  not not_16 (not_16_out, E_PARALELA[2]);
  not not_17 (not_17_out, E_PARALELA[1]);
  not not_18 (not_18_out, E_PARALELA[1]);
  not not_19 (not_19_out, E_PARALELA[0]);
  _7_Segment_Display u_7_segment_display_5 (
    .f(not_17_out), .a(not_18_out), .b(1'b1), .e(not_20_out), .d(not_21_out), .c(1'b1));  // open: g, dp
  _7_Segment_Display u_7_segment_display_6 (
    .f(not_19_out), .a(not_24_out), .b(1'b1), .e(not_22_out), .d(not_23_out), .c(1'b1));  // open: g, dp
  not not_20 (not_20_out, E_PARALELA[1]);
  not not_21 (not_21_out, E_PARALELA[1]);
  not not_22 (not_22_out, E_PARALELA[0]);
  not not_23 (not_23_out, E_PARALELA[0]);
  not not_24 (not_24_out, E_PARALELA[0]);
  FF_JK_ME_PC_D ff_jk_me_pc_d_1 (
    .PRESET(PRESET_out), .J(mux_1_out_7), .CLK(CLK_out), .CLEAR(CLEAR_out), .Q(S_PARALELA[3]),
    .Qq(ff_jk_me_pc_d_1_qq));
  // NoConnect on ff_jk_me_pc_d_1_qq
  _7_Segment_Display u_7_segment_display_7 (
    .f(not_26_out), .a(not_27_out), .b(1'b1), .e(not_25_out), .d(not_28_out), .c(1'b1));  // open: g, dp
  not not_25 (not_25_out, E_SERIAL_ESQ);
  MUX mux_2 (
    .I0(S_PARALELA[2]), .I1(S_PARALELA[1]), .I2(S_PARALELA[3]), .I3(E_PARALELA[2]), .A(SEL[0]), .B(SEL[1]),
    .out_7(mux_2_out_7));
  not not_26 (not_26_out, E_SERIAL_ESQ);
  not not_27 (not_27_out, E_SERIAL_ESQ);
  not not_28 (not_28_out, E_SERIAL_ESQ);
  not not_29 (not_29_out, S_PARALELA[3]);
  not not_30 (not_30_out, S_PARALELA[3]);
  _7_Segment_Display u_7_segment_display_8 (
    .f(not_29_out), .a(not_30_out), .b(1'b1), .e(not_31_out), .d(not_32_out), .c(1'b1));  // open: g, dp
  not not_31 (not_31_out, S_PARALELA[3]);
  not not_32 (not_32_out, S_PARALELA[3]);
  not not_33 (not_33_out, S_PARALELA[2]);
  not not_34 (not_34_out, S_PARALELA[2]);
  not not_35 (not_35_out, S_PARALELA[1]);
  not not_36 (not_36_out, S_PARALELA[1]);
  _7_Segment_Display u_7_segment_display_9 (
    .f(not_33_out), .a(not_34_out), .b(1'b1), .e(not_37_out), .d(not_38_out), .c(1'b1));  // open: g, dp
  _7_Segment_Display u_7_segment_display_10 (
    .f(not_35_out), .a(not_36_out), .b(1'b1), .e(not_39_out), .d(not_40_out), .c(1'b1));  // open: g, dp
  not not_37 (not_37_out, S_PARALELA[2]);
  not not_38 (not_38_out, S_PARALELA[2]);
  not not_39 (not_39_out, S_PARALELA[1]);
  not not_40 (not_40_out, S_PARALELA[1]);
  FF_JK_ME_PC_D ff_jk_me_pc_d_2 (
    .PRESET(PRESET_out), .J(mux_2_out_7), .CLK(CLK_out), .CLEAR(CLEAR_out), .Q(S_PARALELA[2]),
    .Qq(ff_jk_me_pc_d_2_qq));
  // NoConnect on ff_jk_me_pc_d_2_qq
  not not_41 (not_41_out, S_PARALELA[0]);
  not not_42 (not_42_out, S_PARALELA[0]);
  _7_Segment_Display u_7_segment_display_11 (
    .f(not_42_out), .a(not_41_out), .b(1'b1), .e(not_43_out), .d(not_44_out), .c(1'b1));  // open: g, dp
  not not_43 (not_43_out, S_PARALELA[0]);
  not not_44 (not_44_out, S_PARALELA[0]);
  MUX mux_3 (
    .I0(S_PARALELA[1]), .I1(S_PARALELA[0]), .I2(S_PARALELA[2]), .I3(E_PARALELA[1]), .A(SEL[0]), .B(SEL[1]),
    .out_7(mux_3_out_7));
  not not_45 (not_45_out, E_SERIAL_DIR);
  not not_46 (not_46_out, E_SERIAL_DIR);
  _7_Segment_Display u_7_segment_display_12 (
    .f(not_45_out), .a(not_46_out), .b(1'b1), .e(not_47_out), .d(not_48_out), .c(1'b1));  // open: g, dp
  not not_47 (not_47_out, E_SERIAL_DIR);
  not not_48 (not_48_out, E_SERIAL_DIR);
  _7_Segment_Display u_7_segment_display_13 (
    .f(not_50_out), .a(not_51_out), .b(1'b1), .e(not_49_out), .d(not_52_out), .c(1'b1));  // open: g, dp
  not not_49 (not_49_out, S_PARALELA[0]);
  FF_JK_ME_PC_D ff_jk_me_pc_d_3 (
    .PRESET(PRESET_out), .J(mux_3_out_7), .CLK(CLK_out), .CLEAR(CLEAR_out), .Q(S_PARALELA[1]),
    .Qq(ff_jk_me_pc_d_3_qq));
  // NoConnect on ff_jk_me_pc_d_3_qq
  not not_50 (not_50_out, S_PARALELA[0]);
  not not_51 (not_51_out, S_PARALELA[0]);
  not not_52 (not_52_out, S_PARALELA[0]);
  MUX mux_4 (
    .I0(S_PARALELA[0]), .I1(E_SERIAL_DIR), .I2(S_PARALELA[1]), .I3(E_PARALELA[0]), .A(SEL[0]), .B(SEL[1]),
    .out_7(mux_4_out_7));
  FF_JK_ME_PC_D ff_jk_me_pc_d_4 (
    .PRESET(PRESET_out), .J(mux_4_out_7), .CLK(CLK_out), .CLEAR(CLEAR_out), .Q(S_PARALELA[0]),
    .Qq(ff_jk_me_pc_d_4_qq));
  // NoConnect on ff_jk_me_pc_d_4_qq

  assign S_SERIAL = S_PARALELA[0];

  // Other names for the same wires on the sheet: A[1:0] = SEL; B[3:0] = E_PARALELA; C = E_SERIAL_ESQ;
  //   D[3:0] = S_PARALELA; F = S_PARALELA[0]; E = E_SERIAL_DIR

  // Notes on the sheet:
  //   00 - MANTER
  //   01 - SHIFT A ESQ
  //   10 - SHIFT A DIR
  //   11 - CARGA PARALELA
  //   Registrador de Deslocamento Universal com FF_JK_ME_PC_D
  //   SELETOR
  //   ENTRADA PARALELA
  //   ------->
  //   ENTRADA SERIAL ESQ
  //   SAIDA PARALELA
  //   <-------
  //   ENTRADA SERIAL DIR
  //   SAIDA SERIAL
endmodule

module decodificador_hex (
  input  [3:0] in_1,
  output [6:0] out_2
);

  wire and_1_out, and_2_out, and_3_out, and_4_out, and_5_out, and_6_out, and_7_out, and_8_out, and_9_out,
       and_10_out, and_11_out, and_12_out, and_13_out, and_14_out, and_15_out, and_16_out, and_17_out,
       and_18_out, and_19_out, and_20_out, and_21_out, and_22_out, and_23_out, and_24_out, and_25_out,
       and_26_out, and_27_out, and_28_out, and_29_out, and_30_out, and_31_out, and_32_out, and_33_out,
       and_34_out, and_35_out, not_1_out, not_2_out, not_3_out, not_4_out;

  not not_1 (not_1_out, in_1[3]);
  not not_2 (not_2_out, in_1[2]);
  not not_3 (not_3_out, in_1[1]);
  not not_4 (not_4_out, in_1[0]);
  and and_1 (and_1_out, not_2_out, not_4_out);
  and and_2 (and_2_out, not_1_out, in_1[1]);
  and and_3 (and_3_out, not_1_out, in_1[2], in_1[0]);
  and and_4 (and_4_out, in_1[3], not_2_out, not_3_out);
  and and_5 (and_5_out, in_1[3], not_4_out);
  and and_6 (and_6_out, in_1[2], in_1[1]);
  and and_7 (and_7_out, not_1_out, not_3_out, not_4_out);
  and and_8 (and_8_out, not_1_out, in_1[1], in_1[0]);
  and and_9 (and_9_out, not_2_out, not_4_out);
  and and_10 (and_10_out, in_1[3], not_3_out, in_1[0]);
  and and_11 (and_11_out, not_1_out, not_2_out);
  and and_12 (and_12_out, not_1_out, in_1[2]);
  and and_13 (and_13_out, in_1[3], not_2_out);
  and and_14 (and_14_out, not_3_out, in_1[0]);
  and and_15 (and_15_out, not_2_out, not_3_out);
  and and_16 (and_16_out, not_2_out, in_1[0]);
  and and_17 (and_17_out, in_1[2], not_3_out, in_1[0]);
  and and_18 (and_18_out, not_1_out, not_2_out, not_4_out);
  and and_19 (and_19_out, not_2_out, in_1[1], in_1[0]);
  and and_20 (and_20_out, in_1[3], not_3_out);
  and and_21 (and_21_out, in_1[2], in_1[1], not_4_out);
  and and_22 (and_22_out, not_2_out, not_4_out);
  and and_23 (and_23_out, in_1[1], not_4_out);
  and and_24 (and_24_out, in_1[3], in_1[1]);
  and and_25 (and_25_out, in_1[3], in_1[2]);
  and and_26 (and_26_out, not_3_out, not_4_out);
  and and_27 (and_27_out, not_1_out, in_1[2], not_3_out);
  and and_28 (and_28_out, in_1[2], not_4_out);
  and and_29 (and_29_out, in_1[3], not_2_out);
  and and_30 (and_30_out, in_1[3], in_1[1]);
  and and_31 (and_31_out, not_2_out, in_1[1]);
  and and_32 (and_32_out, in_1[3], not_2_out);
  and and_33 (and_33_out, not_1_out, in_1[2], not_3_out);
  and and_34 (and_34_out, in_1[1], not_4_out);
  and and_35 (and_35_out, in_1[3], in_1[0]);
  or or_1 (out_2[0], and_1_out, and_2_out, and_3_out, and_4_out, and_5_out, and_6_out);
  or or_2 (out_2[1], and_7_out, and_8_out, and_9_out, and_10_out, and_11_out);
  or or_3 (out_2[2], and_12_out, and_13_out, and_14_out, and_15_out, and_16_out);
  or or_4 (out_2[3], and_17_out, and_18_out, and_19_out, and_20_out, and_21_out);
  or or_5 (out_2[4], and_22_out, and_23_out, and_24_out, and_25_out);
  or or_6 (out_2[5], and_26_out, and_27_out, and_28_out, and_29_out, and_30_out);
  or or_7 (out_2[6], and_31_out, and_32_out, and_33_out, and_34_out, and_35_out);
endmodule

module Delay (
  input  VALOR_PRESETADO,
  input  ENABLE,
  output PRESET,
  output CLEAR
);

  wire not_1_out;

  not not_1 (not_1_out, VALOR_PRESETADO);
  and and_1 (PRESET, VALOR_PRESETADO, ENABLE);
  and and_2 (CLEAR, not_1_out, ENABLE);
endmodule

module MUX (
  input  A,
  input  B,
  input  I0,
  input  I1,
  input  I2,
  input  I3,
  output out_7
);

  wire and_1_out, and_2_out, and_3_out, and_4_out;

  and and_1 (and_1_out, ~B, I0, ~A);  // AND_Gate
  and and_2 (and_2_out, B, I1, ~A);  // AND_Gate
  and and_3 (and_3_out, ~B, I2, A);  // AND_Gate
  and and_4 (and_4_out, B, I3, A);
  or or_1 (out_7, and_1_out, and_2_out, and_3_out, and_4_out);
endmodule
