// Logisim project Atividade3.circ as structural Verilog
module cortador_de_pulsos_cresc_asinc (
  input  J,
  output out_2,
  output out_3,
  output out_4,
  output out_5
);

  wire CLEAR_out, CLK_out, ff_jk_me_pc_t_1_qq, ff_jk_me_pc_t_2_qq, ff_jk_me_pc_t_3_qq, ff_jk_me_pc_t_4_qq,
       not_1_out, not_2_out, not_3_out, not_4_out, not_5_out, not_6_out, not_7_out, not_8_out, not_9_out,
       not_10_out, not_11_out, not_12_out, not_13_out, not_14_out, not_15_out, not_16_out, not_17_out,
       not_18_out, not_19_out, not_20_out;
  wire [6:0] decodificador_hex_1_out_2;

  not not_1 (not_1_out, J);
  not not_2 (not_2_out, J);
  _7_Segment_Display u_7_segment_display_1 (
    .f(not_1_out), .a(not_2_out), .b(1'b1), .e(not_3_out), .d(not_4_out), .c(1'b1));  // open: g, dp
  not not_3 (not_3_out, J);
  not not_4 (not_4_out, J);
  Button CLEAR (.out(CLEAR_out));
  Clock CLK (.out(CLK_out));
  not not_5 (not_5_out, out_5);
  not not_6 (not_6_out, out_5);
  _7_Segment_Display u_7_segment_display_2 (
    .f(not_5_out), .a(not_6_out), .b(1'b1), .e(not_7_out), .d(not_8_out), .c(1'b1));  // open: g, dp
  not not_7 (not_7_out, out_5);
  not not_8 (not_8_out, out_5);
  not not_9 (not_9_out, out_4);
  not not_10 (not_10_out, out_4);
  _7_Segment_Display u_7_segment_display_3 (
    .f(not_9_out), .a(not_10_out), .b(1'b1), .e(not_11_out), .d(not_12_out), .c(1'b1));  // open: g, dp
  _7_Segment_Display u_7_segment_display_4 (
    .f(not_14_out), .a(not_15_out), .b(1'b1), .e(not_13_out), .d(not_18_out), .c(1'b1));  // open: g, dp
  not not_11 (not_11_out, out_4);
  not not_12 (not_12_out, out_4);
  not not_13 (not_13_out, out_3);
  not not_14 (not_14_out, out_3);
  not not_15 (not_15_out, out_3);
  not not_16 (not_16_out, out_2);
  not not_17 (not_17_out, out_2);
  _7_Segment_Display u_7_segment_display_5 (
    .f(not_16_out), .a(not_17_out), .b(1'b1), .e(not_19_out), .d(not_20_out), .c(1'b1));  // open: g, dp
  not not_18 (not_18_out, out_3);
  not not_19 (not_19_out, out_2);
  not not_20 (not_20_out, out_2);
  FF_JK_ME_PC_T ff_jk_me_pc_t_1 (
    .PRESET(1'b0), .J(J), .CLK(CLK_out), .CLEAR(CLEAR_out), .Q(out_2), .Qq(ff_jk_me_pc_t_1_qq));
  // NoConnect on ff_jk_me_pc_t_1_qq
  decodificador_hex decodificador_hex_1 (.in_1({out_5, out_4, out_3, out_2}), .out_2(decodificador_hex_1_out_2));
  _7_Segment_Display u_7_segment_display_6 (
    .g(decodificador_hex_1_out_2[6]), .f(decodificador_hex_1_out_2[5]), .a(decodificador_hex_1_out_2[0]),
    .b(decodificador_hex_1_out_2[1]), .e(decodificador_hex_1_out_2[4]), .d(decodificador_hex_1_out_2[3]),
    .c(decodificador_hex_1_out_2[2]));  // open: dp
  FF_JK_ME_PC_T ff_jk_me_pc_t_2 (
    .PRESET(1'b0), .J(J), .CLK(out_2), .CLEAR(CLEAR_out), .Q(out_3), .Qq(ff_jk_me_pc_t_2_qq));
  // NoConnect on ff_jk_me_pc_t_2_qq
  FF_JK_ME_PC_T ff_jk_me_pc_t_3 (
    .PRESET(1'b0), .J(J), .CLK(out_3), .CLEAR(CLEAR_out), .Q(out_4), .Qq(ff_jk_me_pc_t_3_qq));
  // NoConnect on ff_jk_me_pc_t_3_qq
  FF_JK_ME_PC_T ff_jk_me_pc_t_4 (
    .PRESET(1'b0), .J(J), .CLK(out_4), .CLEAR(CLEAR_out), .Q(out_5), .Qq(ff_jk_me_pc_t_4_qq));
  // NoConnect on ff_jk_me_pc_t_4_qq

  // Other names for the same wires on the sheet: B = J; S[3:0] = {out_5, out_4, out_3, out_2}

  // Notes on the sheet:
  //   ENTRADA
  //   Contador De Pulsos
  //   SAIDA PARALELA
  //   SAÍDA
endmodule

module cortador_de_decada_cresc_asinc (
  input  J,
  output out_2,
  output out_3,
  output out_4,
  output out_5
);

  wire and_1_out, CLEAR_out, CLK_out, ff_jk_me_pc_t_1_qq, ff_jk_me_pc_t_2_qq, ff_jk_me_pc_t_3_qq, nand_1_out,
       not_1_out, not_2_out, not_3_out, not_4_out, not_5_out, not_6_out, not_7_out, not_8_out, not_9_out,
       not_10_out, not_11_out, not_12_out, not_13_out, not_14_out, not_15_out, not_16_out, not_17_out,
       not_18_out, not_19_out, not_20_out, not_21_out, not_22_out, not_23_out, not_24_out, not_25_out;
  wire [6:0] decodificador_hex_1_out_2;

  not not_1 (not_1_out, J);
  not not_2 (not_2_out, J);
  _7_Segment_Display u_7_segment_display_1 (
    .f(not_1_out), .a(not_2_out), .b(1'b1), .e(not_3_out), .d(not_4_out), .c(1'b1));  // open: g, dp
  not not_3 (not_3_out, J);
  not not_4 (not_4_out, J);
  Button CLEAR (.out(CLEAR_out));
  not not_5 (not_5_out, CLEAR_out);
  Clock CLK (.out(CLK_out));
  not not_6 (not_6_out, and_1_out);
  not not_7 (not_7_out, out_5);
  not not_8 (not_8_out, out_5);
  _7_Segment_Display u_7_segment_display_2 (
    .f(not_7_out), .a(not_8_out), .b(1'b1), .e(not_9_out), .d(not_10_out), .c(1'b1));  // open: g, dp
  not not_9 (not_9_out, out_5);
  not not_10 (not_10_out, out_5);
  not not_11 (not_11_out, out_4);
  not not_12 (not_12_out, out_4);
  _7_Segment_Display u_7_segment_display_3 (
    .f(not_11_out), .a(not_12_out), .b(1'b1), .e(not_13_out), .d(not_14_out), .c(1'b1));  // open: g, dp
  _7_Segment_Display u_7_segment_display_4 (
    .f(not_16_out), .a(not_17_out), .b(1'b1), .e(not_15_out), .d(not_20_out), .c(1'b1));  // open: g, dp
  not not_13 (not_13_out, out_4);
  not not_14 (not_14_out, out_4);
  not not_15 (not_15_out, out_3);
  not not_16 (not_16_out, out_3);
  not not_17 (not_17_out, out_3);
  not not_18 (not_18_out, out_2);
  not not_19 (not_19_out, out_2);
  _7_Segment_Display u_7_segment_display_5 (
    .f(not_18_out), .a(not_19_out), .b(1'b1), .e(not_21_out), .d(not_22_out), .c(1'b1));  // open: g, dp
  not not_20 (not_20_out, out_3);
  not not_21 (not_21_out, out_2);
  not not_22 (not_22_out, out_2);
  FF_JK_ME_PC_T ff_jk_me_pc_t_1 (
    .PRESET(1'b0), .J(J), .CLK(CLK_out), .CLEAR(not_6_out), .Q(out_2), .Qq(ff_jk_me_pc_t_1_qq));
  not not_23 (not_23_out, and_1_out);
  decodificador_hex decodificador_hex_1 (.in_1({out_5, out_4, out_3, out_2}), .out_2(decodificador_hex_1_out_2));
  _7_Segment_Display u_7_segment_display_6 (
    .g(decodificador_hex_1_out_2[6]), .f(decodificador_hex_1_out_2[5]), .a(decodificador_hex_1_out_2[0]),
    .b(decodificador_hex_1_out_2[1]), .e(decodificador_hex_1_out_2[4]), .d(decodificador_hex_1_out_2[3]),
    .c(decodificador_hex_1_out_2[2]));  // open: dp
  FF_JK_ME_PC_T ff_jk_me_pc_t_2 (
    .PRESET(1'b0), .J(J), .CLK(out_2), .CLEAR(not_23_out), .Q(out_3), .Qq(ff_jk_me_pc_t_2_qq));
  not not_24 (not_24_out, and_1_out);
  FF_JK_ME_PC_T ff_jk_me_pc_t_3 (
    .PRESET(1'b0), .J(J), .CLK(out_3), .CLEAR(not_24_out), .Q(out_4), .Qq(ff_jk_me_pc_t_3_qq));
  not not_25 (not_25_out, and_1_out);
  FF_JK_ME_PC_T ff_jk_me_pc_t_4 (.PRESET(1'b0), .J(J), .CLK(out_4), .CLEAR(not_25_out), .Q(out_5));  // open: Qq
  and and_1 (and_1_out, not_5_out, nand_1_out);
  nand nand_1 (nand_1_out, out_2, ff_jk_me_pc_t_2_qq, ff_jk_me_pc_t_3_qq, out_5);

  // Other names for the same wires on the sheet: B = J; S[3:0] = {out_5, out_4, out_3, out_2}

  // Notes on the sheet:
  //   ENTRADA
  //   Contador De Década
  //   SAIDA PARALELA
  //   SAÍDA
endmodule

module cortador_de_n_cresc_asinc (
  input  J,
  input  [3:0] STOP,
  output out_3,
  output out_4,
  output out_5,
  output out_6
);

  wire and_1_out, CLEAR_out, CLK_out, conhecidencia_vetor_1_out_3, not_1_out, not_2_out, not_3_out,
       not_4_out, not_5_out, not_6_out, not_7_out, not_8_out, not_9_out, not_10_out, not_11_out, not_12_out,
       not_13_out, not_14_out, not_15_out, not_16_out, not_17_out, not_18_out, not_19_out, not_20_out,
       not_21_out, not_22_out, not_23_out, not_24_out, not_25_out, not_26_out, not_27_out, not_28_out,
       not_29_out, not_30_out, not_31_out, not_32_out, not_33_out, not_34_out, not_35_out, not_36_out,
       not_37_out, not_38_out, not_39_out, not_40_out, not_41_out;
  wire [6:0] decodificador_hex_1_out_2, decodificador_hex_2_out_2;

  not not_1 (not_1_out, J);
  not not_2 (not_2_out, J);
  _7_Segment_Display u_7_segment_display_1 (
    .f(not_1_out), .a(not_2_out), .b(1'b1), .e(not_3_out), .d(not_4_out), .c(1'b1));  // open: g, dp
  not not_3 (not_3_out, J);
  not not_4 (not_4_out, J);
  Button CLEAR (.out(CLEAR_out));
  not not_5 (not_5_out, CLEAR_out);
  Clock CLK (.out(CLK_out));
  not not_6 (not_6_out, and_1_out);
  not not_7 (not_7_out, out_6);
  not not_8 (not_8_out, out_6);
  _7_Segment_Display u_7_segment_display_2 (
    .f(not_7_out), .a(not_8_out), .b(1'b1), .e(not_9_out), .d(not_10_out), .c(1'b1));  // open: g, dp
  not not_9 (not_9_out, out_6);
  not not_10 (not_10_out, out_6);
  not not_11 (not_11_out, out_5);
  not not_12 (not_12_out, out_5);
  _7_Segment_Display u_7_segment_display_3 (
    .f(not_11_out), .a(not_12_out), .b(1'b1), .e(not_13_out), .d(not_14_out), .c(1'b1));  // open: g, dp
  _7_Segment_Display u_7_segment_display_4 (
    .f(not_16_out), .a(not_17_out), .b(1'b1), .e(not_15_out), .d(not_20_out), .c(1'b1));  // open: g, dp
  not not_13 (not_13_out, out_5);
  not not_14 (not_14_out, out_5);
  not not_15 (not_15_out, out_4);
  not not_16 (not_16_out, out_4);
  not not_17 (not_17_out, out_4);
  not not_18 (not_18_out, out_3);
  not not_19 (not_19_out, out_3);
  _7_Segment_Display u_7_segment_display_5 (
    .f(not_18_out), .a(not_19_out), .b(1'b1), .e(not_21_out), .d(not_22_out), .c(1'b1));  // open: g, dp
  not not_20 (not_20_out, out_4);
  not not_21 (not_21_out, out_3);
  not not_22 (not_22_out, out_3);
  FF_JK_ME_PC_T ff_jk_me_pc_t_1 (.PRESET(1'b0), .J(J), .CLK(CLK_out), .CLEAR(not_6_out), .Q(out_3));  // open: Qq
  not not_23 (not_23_out, and_1_out);
  not not_24 (not_24_out, STOP[3]);
  not not_25 (not_25_out, STOP[3]);
  not not_26 (not_26_out, STOP[2]);
  _7_Segment_Display u_7_segment_display_6 (
    .f(not_24_out), .a(not_25_out), .b(1'b1), .e(not_27_out), .d(not_28_out), .c(1'b1));  // open: g, dp
  _7_Segment_Display u_7_segment_display_7 (
    .f(not_26_out), .a(not_31_out), .b(1'b1), .e(not_29_out), .d(not_30_out), .c(1'b1));  // open: g, dp
  not not_27 (not_27_out, STOP[3]);
  not not_28 (not_28_out, STOP[3]);
  not not_29 (not_29_out, STOP[2]);
  not not_30 (not_30_out, STOP[2]);
  not not_31 (not_31_out, STOP[2]);
  not not_32 (not_32_out, STOP[1]);
  not not_33 (not_33_out, STOP[1]);
  _7_Segment_Display u_7_segment_display_8 (
    .f(not_32_out), .a(not_33_out), .b(1'b1), .e(not_34_out), .d(not_35_out), .c(1'b1));  // open: g, dp
  not not_34 (not_34_out, STOP[1]);
  not not_35 (not_35_out, STOP[1]);
  FF_JK_ME_PC_T ff_jk_me_pc_t_2 (.PRESET(1'b0), .J(J), .CLK(out_3), .CLEAR(not_23_out), .Q(out_4));  // open: Qq
  not not_36 (not_36_out, and_1_out);
  not not_37 (not_37_out, STOP[0]);
  not not_38 (not_38_out, STOP[0]);
  _7_Segment_Display u_7_segment_display_9 (
    .f(not_37_out), .a(not_38_out), .b(1'b1), .e(not_39_out), .d(not_40_out), .c(1'b1));  // open: g, dp
  not not_39 (not_39_out, STOP[0]);
  not not_40 (not_40_out, STOP[0]);
  decodificador_hex decodificador_hex_1 (.in_1({out_6, out_5, out_4, out_3}), .out_2(decodificador_hex_1_out_2));
  FF_JK_ME_PC_T ff_jk_me_pc_t_3 (.PRESET(1'b0), .J(J), .CLK(out_4), .CLEAR(not_36_out), .Q(out_5));  // open: Qq
  _7_Segment_Display u_7_segment_display_10 (
    .g(decodificador_hex_1_out_2[6]), .f(decodificador_hex_1_out_2[5]), .a(decodificador_hex_1_out_2[0]),
    .b(decodificador_hex_1_out_2[1]), .e(decodificador_hex_1_out_2[4]), .d(decodificador_hex_1_out_2[3]),
    .c(decodificador_hex_1_out_2[2]));  // open: dp
  not not_41 (not_41_out, and_1_out);
  decodificador_hex decodificador_hex_2 (.in_1(STOP), .out_2(decodificador_hex_2_out_2));
  FF_JK_ME_PC_T ff_jk_me_pc_t_4 (.PRESET(1'b0), .J(J), .CLK(out_5), .CLEAR(not_41_out), .Q(out_6));  // open: Qq
  _7_Segment_Display u_7_segment_display_11 (
    .g(decodificador_hex_2_out_2[6]), .f(decodificador_hex_2_out_2[5]), .a(decodificador_hex_2_out_2[0]),
    .b(decodificador_hex_2_out_2[1]), .e(decodificador_hex_2_out_2[4]), .d(decodificador_hex_2_out_2[3]),
    .c(decodificador_hex_2_out_2[2]));  // open: dp
  and and_1 (and_1_out, not_5_out, conhecidencia_vetor_1_out_3);
  conhecidencia_vetor conhecidencia_vetor_1 (
    .in_1({out_6, out_5, out_4, out_3}), .in_2(STOP), .out_3(conhecidencia_vetor_1_out_3));

  // Other names for the same wires on the sheet: B = J; S[3:0] = {out_6, out_5, out_4, out_3}; ST[3:0] = STOP

  // Notes on the sheet:
  //   ENTRADA
  //   Contador De N
  //   SAIDA PARALELA
  //   ---->
  //   SAIDA PARALELA
  //   SAÍDA
  //   ---->
  //   SAÍDA
endmodule

module cortador_de_pulsos_decr_asinc (
  input  J,
  output out_2,
  output out_3,
  output out_4,
  output out_5
);

  wire CLK_out, ff_jk_me_pc_t_1_qq, ff_jk_me_pc_t_2_qq, ff_jk_me_pc_t_3_qq, ff_jk_me_pc_t_4_qq, not_1_out,
       not_2_out, not_3_out, not_4_out, not_5_out, not_6_out, not_7_out, not_8_out, not_9_out, not_10_out,
       not_11_out, not_12_out, not_13_out, not_14_out, not_15_out, not_16_out, not_17_out, not_18_out,
       not_19_out, not_20_out, not_21_out, not_22_out, not_23_out, not_24_out, PRESET_out;
  wire [6:0] decodificador_hex_1_out_2;

  not not_1 (not_1_out, J);
  not not_2 (not_2_out, J);
  _7_Segment_Display u_7_segment_display_1 (
    .f(not_1_out), .a(not_2_out), .b(1'b1), .e(not_3_out), .d(not_4_out), .c(1'b1));  // open: g, dp
  not not_3 (not_3_out, J);
  not not_4 (not_4_out, J);
  Button PRESET (.out(PRESET_out));
  Clock CLK (.out(CLK_out));
  not not_5 (not_5_out, CLK_out);
  not not_6 (not_6_out, out_5);
  not not_7 (not_7_out, out_5);
  _7_Segment_Display u_7_segment_display_2 (
    .f(not_6_out), .a(not_7_out), .b(1'b1), .e(not_8_out), .d(not_9_out), .c(1'b1));  // open: g, dp
  not not_8 (not_8_out, out_5);
  not not_9 (not_9_out, out_5);
  not not_10 (not_10_out, out_4);
  not not_11 (not_11_out, out_4);
  _7_Segment_Display u_7_segment_display_3 (
    .f(not_10_out), .a(not_11_out), .b(1'b1), .e(not_12_out), .d(not_13_out), .c(1'b1));  // open: g, dp
  _7_Segment_Display u_7_segment_display_4 (
    .f(not_15_out), .a(not_16_out), .b(1'b1), .e(not_14_out), .d(not_19_out), .c(1'b1));  // open: g, dp
  not not_12 (not_12_out, out_4);
  not not_13 (not_13_out, out_4);
  not not_14 (not_14_out, out_3);
  not not_15 (not_15_out, out_3);
  not not_16 (not_16_out, out_3);
  not not_17 (not_17_out, out_2);
  not not_18 (not_18_out, out_2);
  _7_Segment_Display u_7_segment_display_5 (
    .f(not_17_out), .a(not_18_out), .b(1'b1), .e(not_20_out), .d(not_21_out), .c(1'b1));  // open: g, dp
  not not_19 (not_19_out, out_3);
  not not_20 (not_20_out, out_2);
  not not_21 (not_21_out, out_2);
  FF_JK_ME_PC_T ff_jk_me_pc_t_1 (
    .PRESET(PRESET_out), .J(J), .CLK(not_5_out), .CLEAR(1'b0), .Q(out_2), .Qq(ff_jk_me_pc_t_1_qq));
  // NoConnect on ff_jk_me_pc_t_1_qq
  not not_22 (not_22_out, out_2);
  decodificador_hex decodificador_hex_1 (.in_1({out_5, out_4, out_3, out_2}), .out_2(decodificador_hex_1_out_2));
  _7_Segment_Display u_7_segment_display_6 (
    .g(decodificador_hex_1_out_2[6]), .f(decodificador_hex_1_out_2[5]), .a(decodificador_hex_1_out_2[0]),
    .b(decodificador_hex_1_out_2[1]), .e(decodificador_hex_1_out_2[4]), .d(decodificador_hex_1_out_2[3]),
    .c(decodificador_hex_1_out_2[2]));  // open: dp
  FF_JK_ME_PC_T ff_jk_me_pc_t_2 (
    .PRESET(PRESET_out), .J(J), .CLK(not_22_out), .CLEAR(1'b0), .Q(out_3), .Qq(ff_jk_me_pc_t_2_qq));
  // NoConnect on ff_jk_me_pc_t_2_qq
  not not_23 (not_23_out, out_3);
  FF_JK_ME_PC_T ff_jk_me_pc_t_3 (
    .PRESET(PRESET_out), .J(J), .CLK(not_23_out), .CLEAR(1'b0), .Q(out_4), .Qq(ff_jk_me_pc_t_3_qq));
  // NoConnect on ff_jk_me_pc_t_3_qq
  not not_24 (not_24_out, out_4);
  FF_JK_ME_PC_T ff_jk_me_pc_t_4 (
    .PRESET(PRESET_out), .J(J), .CLK(not_24_out), .CLEAR(1'b0), .Q(out_5), .Qq(ff_jk_me_pc_t_4_qq));
  // NoConnect on ff_jk_me_pc_t_4_qq

  // Other names for the same wires on the sheet: B = J; S[3:0] = {out_5, out_4, out_3, out_2}

  // Notes on the sheet:
  //   ENTRADA
  //   Contador De Pulsos INV
  //   SAIDA PARALELA
  //   SAÍDA
endmodule

module cortador_de_decada_decr_asinc (
  input  J,
  output out_2,
  output out_3,
  output out_4,
  output out_5
);

  wire CLEAR_out, CLK_out, ff_jk_me_pc_t_1_qq, ff_jk_me_pc_t_2_qq, ff_jk_me_pc_t_3_qq, ff_jk_me_pc_t_4_qq,
       nand_1_out, not_1_out, not_2_out, not_3_out, not_4_out, not_5_out, not_6_out, not_7_out, not_8_out,
       not_9_out, not_10_out, not_11_out, not_12_out, not_13_out, not_14_out, not_15_out, not_16_out,
       not_17_out, not_18_out, not_19_out, not_20_out, not_21_out, not_22_out, not_23_out, not_24_out,
       not_25_out, or_1_out, or_2_out, or_3_out, or_4_out;
  wire [6:0] decodificador_hex_1_out_2;

  not not_1 (not_1_out, J);
  not not_2 (not_2_out, J);
  _7_Segment_Display u_7_segment_display_1 (
    .f(not_1_out), .a(not_2_out), .b(1'b1), .e(not_3_out), .d(not_4_out), .c(1'b1));  // open: g, dp
  not not_3 (not_3_out, J);
  not not_4 (not_4_out, J);
  Button CLEAR (.out(CLEAR_out));
  Clock CLK (.out(CLK_out));
  or or_1 (or_1_out, 1'b0, not_25_out);
  not not_5 (not_5_out, CLK_out);
  not not_6 (not_6_out, out_5);
  not not_7 (not_7_out, out_5);
  _7_Segment_Display u_7_segment_display_2 (
    .f(not_6_out), .a(not_7_out), .b(1'b1), .e(not_8_out), .d(not_9_out), .c(1'b1));  // open: g, dp
  not not_8 (not_8_out, out_5);
  not not_9 (not_9_out, out_5);
  not not_10 (not_10_out, out_4);
  not not_11 (not_11_out, out_4);
  _7_Segment_Display u_7_segment_display_3 (
    .f(not_10_out), .a(not_11_out), .b(1'b1), .e(not_12_out), .d(not_13_out), .c(1'b1));  // open: g, dp
  _7_Segment_Display u_7_segment_display_4 (
    .f(not_15_out), .a(not_16_out), .b(1'b1), .e(not_14_out), .d(not_19_out), .c(1'b1));  // open: g, dp
  not not_12 (not_12_out, out_4);
  not not_13 (not_13_out, out_4);
  not not_14 (not_14_out, out_3);
  not not_15 (not_15_out, out_3);
  not not_16 (not_16_out, out_3);
  not not_17 (not_17_out, out_2);
  not not_18 (not_18_out, out_2);
  _7_Segment_Display u_7_segment_display_5 (
    .f(not_17_out), .a(not_18_out), .b(1'b1), .e(not_20_out), .d(not_21_out), .c(1'b1));  // open: g, dp
  not not_19 (not_19_out, out_3);
  not not_20 (not_20_out, out_2);
  not not_21 (not_21_out, out_2);
  or or_2 (or_2_out, CLEAR_out, not_25_out);
  FF_JK_ME_PC_T ff_jk_me_pc_t_1 (
    .PRESET(or_1_out), .J(J), .CLK(not_5_out), .CLEAR(CLEAR_out), .Q(out_2), .Qq(ff_jk_me_pc_t_1_qq));
  not not_22 (not_22_out, out_2);
  decodificador_hex decodificador_hex_1 (.in_1({out_5, out_4, out_3, out_2}), .out_2(decodificador_hex_1_out_2));
  _7_Segment_Display u_7_segment_display_6 (
    .g(decodificador_hex_1_out_2[6]), .f(decodificador_hex_1_out_2[5]), .a(decodificador_hex_1_out_2[0]),
    .b(decodificador_hex_1_out_2[1]), .e(decodificador_hex_1_out_2[4]), .d(decodificador_hex_1_out_2[3]),
    .c(decodificador_hex_1_out_2[2]));  // open: dp
  or or_3 (or_3_out, CLEAR_out, not_25_out);
  FF_JK_ME_PC_T ff_jk_me_pc_t_2 (
    .PRESET(1'b0), .J(J), .CLK(not_22_out), .CLEAR(or_2_out), .Q(out_3), .Qq(ff_jk_me_pc_t_2_qq));
  not not_23 (not_23_out, out_3);
  FF_JK_ME_PC_T ff_jk_me_pc_t_3 (
    .PRESET(1'b0), .J(J), .CLK(not_23_out), .CLEAR(or_3_out), .Q(out_4), .Qq(ff_jk_me_pc_t_3_qq));
  or or_4 (or_4_out, 1'b0, not_25_out);
  not not_24 (not_24_out, out_4);
  FF_JK_ME_PC_T ff_jk_me_pc_t_4 (
    .PRESET(or_4_out), .J(J), .CLK(not_24_out), .CLEAR(CLEAR_out), .Q(out_5), .Qq(ff_jk_me_pc_t_4_qq));
  not not_25 (not_25_out, nand_1_out);
  nand nand_1 (nand_1_out, ff_jk_me_pc_t_1_qq, ff_jk_me_pc_t_2_qq, ff_jk_me_pc_t_3_qq, ff_jk_me_pc_t_4_qq);

  // Other names for the same wires on the sheet: B = J; S[3:0] = {out_5, out_4, out_3, out_2}

  // Notes on the sheet:
  //   ENTRADA
  //   Contador De Década INV
  //   SAIDA PARALELA
  //   SAÍDA
endmodule

module cortador_de_n_decr_asinc (
  input  J,
  input  [3:0] START,
  input  [3:0] in_3,
  output out_4,
  output out_5,
  output out_6,
  output out_7
);

  wire CLEAR_out, CLK_out, conhecidencia_vetor_1_out_3, mux1_1_clr, mux1_1_set, mux1_2_clr, mux1_2_set,
       mux1_3_clr, mux1_3_set, mux1_4_clr, mux1_4_set, not_1_out, not_2_out, not_3_out, not_4_out, not_5_out,
       not_6_out, not_7_out, not_8_out, not_9_out, not_10_out, not_11_out, not_12_out, not_13_out,
       not_14_out, not_15_out, not_16_out, not_17_out, not_18_out, not_19_out, not_20_out, not_21_out,
       not_22_out, not_23_out, not_24_out, not_25_out, not_26_out, not_27_out, not_28_out, not_29_out,
       not_30_out, not_31_out, not_32_out, not_33_out, not_34_out, not_35_out, not_36_out, not_37_out,
       not_38_out, not_39_out, not_40_out, not_41_out, or_1_out, or_2_out, or_3_out, or_4_out, or_5_out;
  wire [3:0] sel_1_out_3;
  wire [6:0] decodificador_hex_1_out_2, decodificador_hex_2_out_2;

  not not_1 (not_1_out, J);
  not not_2 (not_2_out, J);
  _7_Segment_Display u_7_segment_display_1 (
    .f(not_1_out), .a(not_2_out), .b(1'b1), .e(not_3_out), .d(not_4_out), .c(1'b1));  // open: g, dp
  not not_3 (not_3_out, J);
  not not_4 (not_4_out, J);
  Button CLEAR (.out(CLEAR_out));
  Clock CLK (.out(CLK_out));
  MUX1 mux1_1 (.E(sel_1_out_3[0]), .SIG(or_5_out), .CLR(mux1_1_clr), .SET(mux1_1_set));
  not not_5 (not_5_out, out_7);
  not not_6 (not_6_out, out_7);
  _7_Segment_Display u_7_segment_display_2 (
    .f(not_5_out), .a(not_6_out), .b(1'b1), .e(not_7_out), .d(not_8_out), .c(1'b1));  // open: g, dp
  not not_7 (not_7_out, out_7);
  not not_8 (not_8_out, out_7);
  or or_1 (or_1_out, mux1_1_set, 1'b0);
  not not_9 (not_9_out, CLK_out);
  not not_10 (not_10_out, out_6);
  not not_11 (not_11_out, out_6);
  _7_Segment_Display u_7_segment_display_3 (
    .f(not_10_out), .a(not_11_out), .b(1'b1), .e(not_12_out), .d(not_13_out), .c(1'b1));  // open: g, dp
  _7_Segment_Display u_7_segment_display_4 (
    .f(not_15_out), .a(not_16_out), .b(1'b1), .e(not_14_out), .d(not_19_out), .c(1'b1));  // open: g, dp
  not not_12 (not_12_out, out_6);
  not not_13 (not_13_out, out_6);
  not not_14 (not_14_out, out_5);
  not not_15 (not_15_out, out_5);
  not not_16 (not_16_out, out_5);
  not not_17 (not_17_out, out_4);
  not not_18 (not_18_out, out_4);
  _7_Segment_Display u_7_segment_display_5 (
    .f(not_17_out), .a(not_18_out), .b(1'b1), .e(not_20_out), .d(not_21_out), .c(1'b1));  // open: g, dp
  not not_19 (not_19_out, out_5);
  not not_20 (not_20_out, out_4);
  not not_21 (not_21_out, out_4);
  FF_JK_ME_PC_T ff_jk_me_pc_t_1 (.PRESET(or_1_out), .J(J), .CLK(not_9_out), .CLEAR(mux1_1_clr), .Q(out_4));  // open: Qq
  not not_22 (not_22_out, START[3]);
  not not_23 (not_23_out, START[3]);
  not not_24 (not_24_out, START[2]);
  _7_Segment_Display u_7_segment_display_6 (
    .f(not_22_out), .a(not_23_out), .b(1'b1), .e(not_25_out), .d(not_26_out), .c(1'b1));  // open: g, dp
  _7_Segment_Display u_7_segment_display_7 (
    .f(not_24_out), .a(not_30_out), .b(1'b1), .e(not_27_out), .d(not_28_out), .c(1'b1));  // open: g, dp
  not not_25 (not_25_out, START[3]);
  not not_26 (not_26_out, START[3]);
  not not_27 (not_27_out, START[2]);
  not not_28 (not_28_out, START[2]);
  MUX1 mux1_2 (.E(sel_1_out_3[1]), .SIG(or_5_out), .CLR(mux1_2_clr), .SET(mux1_2_set));
  or or_2 (or_2_out, mux1_2_set, 1'b0);
  not not_29 (not_29_out, out_4);
  not not_30 (not_30_out, START[2]);
  not not_31 (not_31_out, START[1]);
  not not_32 (not_32_out, START[1]);
  _7_Segment_Display u_7_segment_display_8 (
    .f(not_31_out), .a(not_32_out), .b(1'b1), .e(not_33_out), .d(not_34_out), .c(1'b1));  // open: g, dp
  not not_33 (not_33_out, START[1]);
  not not_34 (not_34_out, START[1]);
  not not_35 (not_35_out, START[0]);
  not not_36 (not_36_out, START[0]);
  _7_Segment_Display u_7_segment_display_9 (
    .f(not_35_out), .a(not_36_out), .b(1'b1), .e(not_37_out), .d(not_38_out), .c(1'b1));  // open: g, dp
  not not_37 (not_37_out, START[0]);
  not not_38 (not_38_out, START[0]);
  FF_JK_ME_PC_T ff_jk_me_pc_t_2 (
    .PRESET(or_2_out), .J(J), .CLK(not_29_out), .CLEAR(mux1_2_clr), .Q(out_5));  // open: Qq
  decodificador_hex decodificador_hex_1 (.in_1({out_7, out_6, out_5, out_4}), .out_2(decodificador_hex_1_out_2));
  MUX1 mux1_3 (.E(sel_1_out_3[2]), .SIG(or_5_out), .CLR(mux1_3_clr), .SET(mux1_3_set));
  or or_3 (or_3_out, mux1_3_set, 1'b0);
  not not_39 (not_39_out, out_5);
  _7_Segment_Display u_7_segment_display_10 (
    .g(decodificador_hex_1_out_2[6]), .f(decodificador_hex_1_out_2[5]), .a(decodificador_hex_1_out_2[0]),
    .b(decodificador_hex_1_out_2[1]), .e(decodificador_hex_1_out_2[4]), .d(decodificador_hex_1_out_2[3]),
    .c(decodificador_hex_1_out_2[2]));  // open: dp
  decodificador_hex decodificador_hex_2 (.in_1(START), .out_2(decodificador_hex_2_out_2));
  FF_JK_ME_PC_T ff_jk_me_pc_t_3 (
    .PRESET(or_3_out), .J(J), .CLK(not_39_out), .CLEAR(mux1_3_clr), .Q(out_6));  // open: Qq
  _7_Segment_Display u_7_segment_display_11 (
    .g(decodificador_hex_2_out_2[6]), .f(decodificador_hex_2_out_2[5]), .a(decodificador_hex_2_out_2[0]),
    .b(decodificador_hex_2_out_2[1]), .e(decodificador_hex_2_out_2[4]), .d(decodificador_hex_2_out_2[3]),
    .c(decodificador_hex_2_out_2[2]));  // open: dp
  MUX1 mux1_4 (.E(sel_1_out_3[3]), .SIG(or_5_out), .CLR(mux1_4_clr), .SET(mux1_4_set));
  or or_4 (or_4_out, mux1_4_set, 1'b0);
  not not_40 (not_40_out, out_6);
  FF_JK_ME_PC_T ff_jk_me_pc_t_4 (
    .PRESET(or_4_out), .J(J), .CLK(not_40_out), .CLEAR(mux1_4_clr), .Q(out_7));  // open: Qq
  SEL sel_1 (.out_3(sel_1_out_3), .in_1(START), .in_2(or_5_out));
  conhecidencia_vetor conhecidencia_vetor_1 (
    .in_1({out_7, out_6, out_5, out_4}), .in_2(in_3), .out_3(conhecidencia_vetor_1_out_3));
  or or_5 (or_5_out, CLEAR_out, not_41_out);
  not not_41 (not_41_out, conhecidencia_vetor_1_out_3);

  // Other names for the same wires on the sheet: B = J; S[3:0] = {out_7, out_6, out_5, out_4}; ST[3:0] = START

  // Notes on the sheet:
  //   ENTRADA
  //   Contador De N INV
  //   SAIDA PARALELA
  //   ---->
  //   SAIDA PARALELA
  //   SAÍDA
  //   ---->
  //   SAÍDA
endmodule

module cortador_com_chave_asinc (
  input  J,
  input  [3:0] STOP,
  input  [3:0] START,
  input  KEY
);

  wire and_1_out, and_2_out, and_3_out, and_4_out, CLEAR_out, CLK_out, conhecidencia_vetor_1_out_3,
       conhecidencia_vetor_2_out_3, mux1_1_clr, mux1_1_set, mux1_2_clr, mux1_2_set, mux1_3_clr, mux1_3_set,
       mux1_4_clr, mux1_4_set, not_1_out, not_2_out, not_3_out, not_4_out, not_5_out, not_6_out, not_7_out,
       not_8_out, not_9_out, not_10_out, not_11_out, not_12_out, not_13_out, not_14_out, not_15_out,
       not_16_out, not_17_out, not_18_out, not_19_out, not_20_out, not_21_out, not_22_out, not_23_out,
       not_24_out, not_25_out, not_26_out, not_27_out, not_28_out, not_29_out, not_30_out, not_31_out,
       not_32_out, not_33_out, not_34_out, not_35_out, not_36_out, not_37_out, not_38_out, not_39_out,
       not_40_out, not_41_out, not_42_out, not_43_out, not_44_out, not_45_out, not_46_out, not_47_out,
       not_48_out, not_49_out, not_50_out, not_51_out, not_52_out, not_53_out, not_54_out, or_1_out,
       or_2_out, or_3_out, or_4_out, or_6_out, or_7_out, or_8_out, xor_1_out, xor_2_out, xor_3_out, xor_4_out;
  wire [3:0] or_5_out, S, sel_1_out_3, sel_2_out_3;
  wire [6:0] decodificador_hex_1_out_2, decodificador_hex_2_out_2, decodificador_hex_3_out_2;

  not not_1 (not_1_out, J);
  not not_2 (not_2_out, J);
  _7_Segment_Display u_7_segment_display_1 (
    .f(not_1_out), .a(not_2_out), .b(1'b1), .e(not_3_out), .d(not_4_out), .c(1'b1));  // open: g, dp
  not not_3 (not_3_out, J);
  not not_4 (not_4_out, J);
  Clock CLK (.out(CLK_out));
  Button CLEAR (.out(CLEAR_out));
  MUX1 mux1_1 (.E(or_5_out[0]), .SIG(or_6_out), .CLR(mux1_1_clr), .SET(mux1_1_set));
  xor xor_1 (xor_1_out, CLK_out, KEY);
  not not_5 (not_5_out, START[3]);
  not not_6 (not_6_out, START[3]);
  _7_Segment_Display u_7_segment_display_2 (
    .f(not_5_out), .a(not_6_out), .b(1'b1), .e(not_7_out), .d(not_8_out), .c(1'b1));  // open: g, dp
  not not_7 (not_7_out, START[3]);
  not not_8 (not_8_out, START[3]);
  or or_1 (or_1_out, mux1_1_set, 1'b0);
  not not_9 (not_9_out, START[2]);
  not not_10 (not_10_out, START[2]);
  not not_11 (not_11_out, START[1]);
  not not_12 (not_12_out, START[1]);
  _7_Segment_Display u_7_segment_display_3 (
    .f(not_9_out), .a(not_10_out), .b(1'b1), .e(not_13_out), .d(not_14_out), .c(1'b1));  // open: g, dp
  _7_Segment_Display u_7_segment_display_4 (
    .f(not_11_out), .a(not_12_out), .b(1'b1), .e(not_15_out), .d(not_16_out), .c(1'b1));  // open: g, dp
  not not_13 (not_13_out, START[2]);
  not not_14 (not_14_out, START[2]);
  not not_15 (not_15_out, START[1]);
  not not_16 (not_16_out, START[1]);
  not not_17 (not_17_out, START[0]);
  not not_18 (not_18_out, START[0]);
  _7_Segment_Display u_7_segment_display_5 (
    .f(not_17_out), .a(not_18_out), .b(1'b1), .e(not_19_out), .d(not_20_out), .c(1'b1));  // open: g, dp
  not not_19 (not_19_out, START[0]);
  not not_20 (not_20_out, START[0]);
  FF_JK_ME_PC_T ff_jk_me_pc_t_1 (.PRESET(or_1_out), .J(J), .CLK(xor_1_out), .CLEAR(mux1_1_clr), .Q(S[0]));  // open: Qq
  xor xor_2 (xor_2_out, S[0], KEY);
  not not_21 (not_21_out, S[3]);
  not not_22 (not_22_out, S[3]);
  not not_23 (not_23_out, S[2]);
  not not_24 (not_24_out, S[2]);
  _7_Segment_Display u_7_segment_display_6 (
    .f(not_21_out), .a(not_22_out), .b(1'b1), .e(not_25_out), .d(not_26_out), .c(1'b1));  // open: g, dp
  _7_Segment_Display u_7_segment_display_7 (
    .f(not_23_out), .a(not_24_out), .b(1'b1), .e(not_27_out), .d(not_28_out), .c(1'b1));  // open: g, dp
  not not_25 (not_25_out, S[3]);
  not not_26 (not_26_out, S[3]);
  not not_27 (not_27_out, S[2]);
  not not_28 (not_28_out, S[2]);
  MUX1 mux1_2 (.E(or_5_out[1]), .SIG(or_6_out), .CLR(mux1_2_clr), .SET(mux1_2_set));
  or or_2 (or_2_out, mux1_2_set, 1'b0);
  not not_29 (not_29_out, S[1]);
  not not_30 (not_30_out, S[1]);
  _7_Segment_Display u_7_segment_display_8 (
    .f(not_29_out), .a(not_30_out), .b(1'b1), .e(not_31_out), .d(not_32_out), .c(1'b1));  // open: g, dp
  _7_Segment_Display u_7_segment_display_9 (
    .f(not_34_out), .a(not_35_out), .b(1'b1), .e(not_33_out), .d(not_36_out), .c(1'b1));  // open: g, dp
  not not_31 (not_31_out, S[1]);
  not not_32 (not_32_out, S[1]);
  not not_33 (not_33_out, S[0]);
  not not_34 (not_34_out, S[0]);
  not not_35 (not_35_out, S[0]);
  not not_36 (not_36_out, S[0]);
  not not_37 (not_37_out, STOP[3]);
  not not_38 (not_38_out, STOP[3]);
  _7_Segment_Display u_7_segment_display_10 (
    .f(not_37_out), .a(not_38_out), .b(1'b1), .e(not_39_out), .d(not_40_out), .c(1'b1));  // open: g, dp
  not not_39 (not_39_out, STOP[3]);
  not not_40 (not_40_out, STOP[3]);
  FF_JK_ME_PC_T ff_jk_me_pc_t_2 (.PRESET(or_2_out), .J(J), .CLK(xor_2_out), .CLEAR(mux1_2_clr), .Q(S[1]));  // open: Qq
  not not_41 (not_41_out, STOP[2]);
  not not_42 (not_42_out, STOP[2]);
  not not_43 (not_43_out, STOP[1]);
  _7_Segment_Display u_7_segment_display_11 (
    .f(not_41_out), .a(not_42_out), .b(1'b1), .e(not_44_out), .d(not_45_out), .c(1'b1));  // open: g, dp
  _7_Segment_Display u_7_segment_display_12 (
    .f(not_43_out), .a(not_50_out), .b(1'b1), .e(not_46_out), .d(not_47_out), .c(1'b1));  // open: g, dp
  not not_44 (not_44_out, STOP[2]);
  not not_45 (not_45_out, STOP[2]);
  not not_46 (not_46_out, STOP[1]);
  not not_47 (not_47_out, STOP[1]);
  MUX1 mux1_3 (.E(or_5_out[2]), .SIG(or_6_out), .CLR(mux1_3_clr), .SET(mux1_3_set));
  or or_3 (or_3_out, mux1_3_set, 1'b0);
  xor xor_3 (xor_3_out, S[1], KEY);
  not not_48 (not_48_out, STOP[0]);
  not not_49 (not_49_out, STOP[0]);
  not not_50 (not_50_out, STOP[1]);
  _7_Segment_Display u_7_segment_display_13 (
    .f(not_48_out), .a(not_49_out), .b(1'b1), .e(not_52_out), .d(not_51_out), .c(1'b1));  // open: g, dp
  not not_51 (not_51_out, STOP[0]);
  not not_52 (not_52_out, STOP[0]);
  decodificador_hex decodificador_hex_1 (.in_1(START), .out_2(decodificador_hex_1_out_2));
  FF_JK_ME_PC_T ff_jk_me_pc_t_3 (.PRESET(or_3_out), .J(J), .CLK(xor_3_out), .CLEAR(mux1_3_clr), .Q(S[2]));  // open: Qq
  _7_Segment_Display u_7_segment_display_14 (
    .g(decodificador_hex_1_out_2[6]), .f(decodificador_hex_1_out_2[5]), .a(decodificador_hex_1_out_2[0]),
    .b(decodificador_hex_1_out_2[1]), .e(decodificador_hex_1_out_2[4]), .d(decodificador_hex_1_out_2[3]),
    .c(decodificador_hex_1_out_2[2]));  // open: dp
  MUX1 mux1_4 (.E(or_5_out[3]), .SIG(or_6_out), .CLR(mux1_4_clr), .SET(mux1_4_set));
  or or_4 (or_4_out, mux1_4_set, 1'b0);
  xor xor_4 (xor_4_out, S[2], KEY);
  decodificador_hex decodificador_hex_2 (.in_1(S), .out_2(decodificador_hex_2_out_2));
  _7_Segment_Display u_7_segment_display_15 (
    .g(decodificador_hex_2_out_2[6]), .f(decodificador_hex_2_out_2[5]), .a(decodificador_hex_2_out_2[0]),
    .b(decodificador_hex_2_out_2[1]), .e(decodificador_hex_2_out_2[4]), .d(decodificador_hex_2_out_2[3]),
    .c(decodificador_hex_2_out_2[2]));  // open: dp
  FF_JK_ME_PC_T ff_jk_me_pc_t_4 (.PRESET(or_4_out), .J(J), .CLK(xor_4_out), .CLEAR(mux1_4_clr), .Q(S[3]));  // open: Qq
  decodificador_hex decodificador_hex_3 (.in_1(STOP), .out_2(decodificador_hex_3_out_2));
  _7_Segment_Display u_7_segment_display_16 (
    .g(decodificador_hex_3_out_2[6]), .f(decodificador_hex_3_out_2[5]), .a(decodificador_hex_3_out_2[0]),
    .b(decodificador_hex_3_out_2[1]), .e(decodificador_hex_3_out_2[4]), .d(decodificador_hex_3_out_2[3]),
    .c(decodificador_hex_3_out_2[2]));  // open: dp
  assign or_5_out = sel_1_out_3 | sel_2_out_3;  // OR_Gate or_5, 4 bits wide
  SEL sel_1 (.out_3(sel_1_out_3), .in_1(START), .in_2(or_7_out));
  SEL sel_2 (.out_3(sel_2_out_3), .in_1(STOP), .in_2(or_8_out));
  and and_1 (and_1_out, CLEAR_out, ~KEY);  // AND_Gate
  and and_2 (and_2_out, CLEAR_out, KEY);
  conhecidencia_vetor conhecidencia_vetor_1 (.in_1(S), .in_2(STOP), .out_3(conhecidencia_vetor_1_out_3));
  conhecidencia_vetor conhecidencia_vetor_2 (.in_1(S), .in_2(START), .out_3(conhecidencia_vetor_2_out_3));
  or or_6 (or_6_out, or_7_out, or_8_out);
  or or_7 (or_7_out, and_1_out, and_3_out);
  or or_8 (or_8_out, and_2_out, and_4_out);
  and and_3 (and_3_out, not_53_out, ~KEY);  // AND_Gate
  and and_4 (and_4_out, not_54_out, KEY);
  not not_53 (not_53_out, conhecidencia_vetor_1_out_3);
  not not_54 (not_54_out, conhecidencia_vetor_2_out_3);

  // Other names for the same wires on the sheet: B = J; SP[3:0] = START; ST[3:0] = STOP

  // Notes on the sheet:
  //   ENTRADA
  //   Contador Com Chave
  //   START
  //   ---->
  //   SAIDA PARALELA
  //   ---->
  //   STOP
  //   START/STOP
  //   ---->
  //   SAIDA SERIAL
  //   ---->
  //   STOP/START
endmodule

module cortador_de_pulsos_cresc_sinc (
  input  [3:0] in_1
);

  wire CLEAR_out, CLK_out, J0, J1, J2, J3, K0, K1, K2, K3, not_1_out, not_2_out, not_3_out, not_4_out,
       not_5_out, not_6_out, not_7_out, not_8_out, not_9_out, not_10_out, not_11_out, not_12_out, not_13_out,
       not_14_out, not_15_out, not_16_out, PRESET_out, Q0, Q1, Q2, Q3;
  wire [6:0] decodificador_hex_1_out_2;

  Button PRESET (.out(PRESET_out));
  Button CLEAR (.out(CLEAR_out));
  Clock CLK (.out(CLK_out));
  not not_1 (not_1_out, Q3);
  not not_2 (not_2_out, Q3);
  _7_Segment_Display u_7_segment_display_1 (
    .f(not_1_out), .a(not_2_out), .b(1'b1), .e(not_3_out), .d(not_4_out), .c(1'b1));  // open: g, dp
  not not_3 (not_3_out, Q3);
  not not_4 (not_4_out, Q3);
  not not_5 (not_5_out, Q2);
  not not_6 (not_6_out, Q2);
  _7_Segment_Display u_7_segment_display_2 (
    .f(not_5_out), .a(not_6_out), .b(1'b1), .e(not_7_out), .d(not_8_out), .c(1'b1));  // open: g, dp
  _7_Segment_Display u_7_segment_display_3 (
    .f(not_10_out), .a(not_11_out), .b(1'b1), .e(not_9_out), .d(not_14_out), .c(1'b1));  // open: g, dp
  not not_7 (not_7_out, Q2);
  not not_8 (not_8_out, Q2);
  not not_9 (not_9_out, Q1);
  FF_JK_ME_PC ff_jk_me_pc_1 (
    .PRESET(PRESET_out), .J(J0), .CLK(CLK_out), .K(K0), .CLEAR(CLEAR_out), .Q(Q0));  // open: Qq
  not not_10 (not_10_out, Q1);
  not not_11 (not_11_out, Q1);
  not not_12 (not_12_out, Q0);
  not not_13 (not_13_out, Q0);
  _7_Segment_Display u_7_segment_display_4 (
    .f(not_12_out), .a(not_13_out), .b(1'b1), .e(not_15_out), .d(not_16_out), .c(1'b1));  // open: g, dp
  not not_14 (not_14_out, Q1);
  not not_15 (not_15_out, Q0);
  not not_16 (not_16_out, Q0);
  decodificador_hex decodificador_hex_1 (.in_1({Q3, Q2, Q1, Q0}), .out_2(decodificador_hex_1_out_2));
  _7_Segment_Display u_7_segment_display_5 (
    .g(decodificador_hex_1_out_2[6]), .f(decodificador_hex_1_out_2[5]), .a(decodificador_hex_1_out_2[0]),
    .b(decodificador_hex_1_out_2[1]), .e(decodificador_hex_1_out_2[4]), .d(decodificador_hex_1_out_2[3]),
    .c(decodificador_hex_1_out_2[2]));  // open: dp
  FF_JK_ME_PC ff_jk_me_pc_2 (
    .PRESET(PRESET_out), .J(J1), .CLK(CLK_out), .K(K1), .CLEAR(CLEAR_out), .Q(Q1));  // open: Qq
  contador_de_pulsos_tabela contador_de_pulsos_tabela_1 (
    .Q0(Q3), .Q1(Q2), .Q2(Q1), .Q3(Q0), .N(in_1), .J0(J3), .K0(K3), .J1(J2), .K1(K2), .J2(J1), .K2(K1),
    .J3(J0), .K3(K0));
  FF_JK_ME_PC ff_jk_me_pc_3 (
    .PRESET(PRESET_out), .J(J2), .CLK(CLK_out), .K(K2), .CLEAR(CLEAR_out), .Q(Q2));  // open: Qq
  FF_JK_ME_PC ff_jk_me_pc_4 (
    .PRESET(PRESET_out), .J(J3), .CLK(CLK_out), .K(K3), .CLEAR(CLEAR_out), .Q(Q3));  // open: Qq

  // Other names for the same wires on the sheet: S[3:0] = {Q3, Q2, Q1, Q0}

  // Notes on the sheet:
  //   Contador De Pulsos
  //   SAIDA PARALELA
  //   SAÍDA
endmodule

module contador_de_pulsos_tabela (
  input  Q0,
  input  Q1,
  input  Q2,
  input  Q3,
  input  [3:0] N,
  output J0,
  output K0,
  output J1,
  output K1,
  output J2,
  output K2,
  output J3,
  output K3
);

  wire and_2_out, and_3_out, and_4_out, and_5_out, and_6_out, and_7_out, and_8_out, and_9_out, and_10_out,
       and_11_out, and_12_out, and_13_out, and_14_out, and_15_out, and_16_out, and_17_out, and_18_out,
       and_19_out, and_20_out, and_21_out, and_22_out, and_23_out, and_24_out, and_25_out, and_26_out,
       and_27_out, and_28_out, and_29_out, not_1_out, not_2_out, not_3_out, not_4_out, not_5_out, not_6_out,
       not_7_out;

  not not_1 (not_1_out, Q0);
  not not_2 (not_2_out, Q1);
  not not_3 (not_3_out, Q2);
  not not_4 (not_4_out, N[3]);
  not not_5 (not_5_out, N[2]);
  not not_6 (not_6_out, N[1]);
  not not_7 (not_7_out, N[0]);
  and and_1 (J0, Q1, Q2, Q3, N[3]);
  and and_2 (and_2_out, not_5_out, not_6_out, not_7_out);
  and and_3 (and_3_out, Q3, not_5_out, not_6_out);
  and and_4 (and_4_out, Q2, not_5_out, not_7_out);
  and and_5 (and_5_out, Q2, Q3, not_5_out);
  and and_6 (and_6_out, Q1, not_6_out, not_7_out);
  and and_7 (and_7_out, Q1, Q3, not_6_out);
  and and_8 (and_8_out, Q1, Q2, not_7_out);
  and and_9 (and_9_out, Q1, Q2, Q3);
  and and_10 (and_10_out, Q2, Q3, N[2]);
  and and_11 (and_11_out, not_1_out, Q2, Q3, N[3]);
  and and_12 (and_12_out, not_4_out, not_6_out, not_7_out);
  and and_13 (and_13_out, Q2, not_4_out, not_7_out);
  and and_14 (and_14_out, Q0, not_6_out, not_7_out);
  and and_15 (and_15_out, Q0, Q2, not_7_out);
  and and_16 (and_16_out, Q3, not_4_out, not_6_out);
  and and_17 (and_17_out, Q2, Q3);
  and and_18 (and_18_out, Q0, Q3, not_6_out);
  and and_19 (and_19_out, Q3, N[1]);
  and and_20 (and_20_out, not_2_out, Q3, N[2]);
  and and_21 (and_21_out, not_1_out, Q3, N[3]);
  and and_22 (and_22_out, not_4_out, not_5_out, not_7_out);
  and and_23 (and_23_out, Q1, not_4_out, not_7_out);
  and and_24 (and_24_out, Q0, not_5_out, not_7_out);
  and and_25 (and_25_out, Q0, Q1, not_7_out);
  and and_26 (and_26_out, Q2, Q3);
  and and_27 (and_27_out, not_2_out, N[2]);
  and and_28 (and_28_out, not_1_out, N[3]);
  and and_29 (and_29_out, not_3_out, N[1]);
  or or_1 (K0, and_2_out, and_3_out, and_4_out, and_5_out, and_6_out, and_7_out, and_8_out, and_9_out);
  or or_2 (J1, and_10_out, and_11_out);
  or or_3 (K1, and_12_out, and_13_out, and_14_out, and_15_out, and_16_out, and_17_out, and_18_out);
  or or_4 (J2, and_19_out, and_20_out, and_21_out);
  or or_5 (K2, and_22_out, and_23_out, and_24_out, and_25_out, and_26_out);
  or or_6 (J3, N[0], and_27_out, and_28_out, and_29_out);

  assign K3 = Q3;
endmodule

module cortador_de_decada_cresc_sinc (
  input  [3:0] in_1
);

  wire CLEAR_out, CLK_out, J0, J1, J2, J3, K0, K1, K2, K3, not_1_out, not_2_out, not_3_out, not_4_out,
       not_5_out, not_6_out, not_7_out, not_8_out, not_9_out, not_10_out, not_11_out, not_12_out, not_13_out,
       not_14_out, not_15_out, not_16_out, PRESET_out, Q0, Q1, Q2, Q3;
  wire [6:0] decodificador_hex_1_out_2;

  Button PRESET (.out(PRESET_out));
  Button CLEAR (.out(CLEAR_out));
  Clock CLK (.out(CLK_out));
  not not_1 (not_1_out, Q3);
  not not_2 (not_2_out, Q3);
  _7_Segment_Display u_7_segment_display_1 (
    .f(not_1_out), .a(not_2_out), .b(1'b1), .e(not_3_out), .d(not_4_out), .c(1'b1));  // open: g, dp
  not not_3 (not_3_out, Q3);
  not not_4 (not_4_out, Q3);
  not not_5 (not_5_out, Q2);
  not not_6 (not_6_out, Q2);
  _7_Segment_Display u_7_segment_display_2 (
    .f(not_5_out), .a(not_6_out), .b(1'b1), .e(not_7_out), .d(not_8_out), .c(1'b1));  // open: g, dp
  _7_Segment_Display u_7_segment_display_3 (
    .f(not_10_out), .a(not_11_out), .b(1'b1), .e(not_9_out), .d(not_14_out), .c(1'b1));  // open: g, dp
  not not_7 (not_7_out, Q2);
  not not_8 (not_8_out, Q2);
  not not_9 (not_9_out, Q1);
  FF_JK_ME_PC ff_jk_me_pc_1 (
    .PRESET(PRESET_out), .J(J0), .CLK(CLK_out), .K(K0), .CLEAR(CLEAR_out), .Q(Q0));  // open: Qq
  not not_10 (not_10_out, Q1);
  not not_11 (not_11_out, Q1);
  not not_12 (not_12_out, Q0);
  not not_13 (not_13_out, Q0);
  _7_Segment_Display u_7_segment_display_4 (
    .f(not_12_out), .a(not_13_out), .b(1'b1), .e(not_15_out), .d(not_16_out), .c(1'b1));  // open: g, dp
  not not_14 (not_14_out, Q1);
  not not_15 (not_15_out, Q0);
  not not_16 (not_16_out, Q0);
  decodificador_hex decodificador_hex_1 (.in_1({Q3, Q2, Q1, Q0}), .out_2(decodificador_hex_1_out_2));
  _7_Segment_Display u_7_segment_display_5 (
    .g(decodificador_hex_1_out_2[6]), .f(decodificador_hex_1_out_2[5]), .a(decodificador_hex_1_out_2[0]),
    .b(decodificador_hex_1_out_2[1]), .e(decodificador_hex_1_out_2[4]), .d(decodificador_hex_1_out_2[3]),
    .c(decodificador_hex_1_out_2[2]));  // open: dp
  FF_JK_ME_PC ff_jk_me_pc_2 (
    .PRESET(PRESET_out), .J(J1), .CLK(CLK_out), .K(K1), .CLEAR(CLEAR_out), .Q(Q1));  // open: Qq
  contador_de_pulsos_tabela contador_de_pulsos_tabela_1 (
    .Q0(Q3), .Q1(Q2), .Q2(Q1), .Q3(Q0), .N(in_1), .J0(J3), .K0(K3), .J1(J2), .K1(K2), .J2(J1), .K2(K1),
    .J3(J0), .K3(K0));
  FF_JK_ME_PC ff_jk_me_pc_3 (
    .PRESET(PRESET_out), .J(J2), .CLK(CLK_out), .K(K2), .CLEAR(CLEAR_out), .Q(Q2));  // open: Qq
  FF_JK_ME_PC ff_jk_me_pc_4 (
    .PRESET(PRESET_out), .J(J3), .CLK(CLK_out), .K(K3), .CLEAR(CLEAR_out), .Q(Q3));  // open: Qq

  // Other names for the same wires on the sheet: S[3:0] = {Q3, Q2, Q1, Q0}

  // Notes on the sheet:
  //   Contador De Década
  //   SAIDA PARALELA
  //   SAÍDA
endmodule

module FF_RS (
  input  set,
  input  clock,
  input  reset,
  output Q,
  output Ql
);

  wire nand_1_out, nand_2_out;

  nand nand_1 (nand_1_out, set, clock);
  nand nand_2 (nand_2_out, clock, reset);
  nand nand_3 (Q, nand_1_out, Ql);
  nand nand_4 (Ql, Q, nand_2_out);

  // Notes on the sheet:
  //   Flip-Flop Reset Set c/ Clock
endmodule

module FF_JK (
  input  J,
  input  clock,
  input  K,
  output Q,
  output Ql
);

  wire nand_1_out, nand_2_out;

  nand nand_1 (nand_1_out, J, clock, Ql);
  nand nand_2 (nand_2_out, Q, clock, K);
  nand nand_3 (Q, nand_1_out, Ql);
  nand nand_4 (Ql, Q, nand_2_out);

  // Notes on the sheet:
  //   Flip-Flop JK
endmodule

module FF_JK_PC (
  input  preset,
  input  J,
  input  clock,
  input  K,
  input  clear,
  output Q,
  output Ql
);

  wire nand_1_out, nand_2_out, not_1_out, not_2_out;

  not not_1 (not_1_out, preset);
  nand nand_1 (nand_1_out, J, clock, Ql);
  nand nand_2 (nand_2_out, Q, clock, K);
  not not_2 (not_2_out, clear);
  nand nand_3 (Q, not_1_out, nand_1_out, Ql);
  nand nand_4 (Ql, Q, nand_2_out, not_2_out);

  // Notes on the sheet:
  //   Flip-Flop JK com Entrada Preset e Clear
endmodule

module FF_JK_ME_PC (
  input  PRESET,
  input  J,
  input  CLK,
  input  K,
  input  CLEAR,
  output Q,
  output Qq
);

  wire nand_1_out, nand_2_out, nand_3_out, nand_4_out, nand_5_out, nand_6_out, not_1_out, not_2_out,
       not_3_out, not_4_out;

  not not_1 (not_1_out, CLK);
  nand nand_1 (nand_1_out, Qq, J, not_1_out);
  nand nand_2 (nand_2_out, not_1_out, K, Q);
  not not_2 (not_2_out, PRESET);
  not not_3 (not_3_out, CLEAR);
  nand nand_3 (nand_3_out, not_2_out, nand_1_out, nand_4_out);
  not not_4 (not_4_out, not_1_out);
  nand nand_4 (nand_4_out, nand_3_out, nand_2_out, not_3_out);
  nand nand_5 (nand_5_out, nand_3_out, not_4_out, not_3_out);
  nand nand_6 (nand_6_out, not_2_out, not_4_out, nand_4_out);
  nand nand_7 (Q, not_2_out, nand_5_out, Qq);
  nand nand_8 (Qq, Q, nand_6_out, not_3_out);

  // Notes on the sheet:
  //   Flip-Flop JK Mestre-Escravo com Entrada Preset e Clear
endmodule

module FF_JK_ME_PC_D (
  input  PRESET,
  input  J,
  input  CLK,
  input  CLEAR,
  output Q,
  output Qq
);

  wire nand_1_out, nand_2_out, nand_3_out, nand_4_out, nand_5_out, nand_6_out, not_1_out, not_2_out,
       not_3_out, not_4_out, not_5_out;

  not not_1 (not_1_out, J);
  not not_2 (not_2_out, CLK);
  nand nand_1 (nand_1_out, Qq, J, not_2_out);
  nand nand_2 (nand_2_out, not_2_out, not_1_out, Q);
  not not_3 (not_3_out, PRESET);
  not not_4 (not_4_out, CLEAR);
  nand nand_3 (nand_3_out, not_3_out, nand_1_out, nand_4_out);
  not not_5 (not_5_out, not_2_out);
  nand nand_4 (nand_4_out, nand_3_out, nand_2_out, not_4_out);
  nand nand_5 (nand_5_out, nand_3_out, not_5_out, not_4_out);
  nand nand_6 (nand_6_out, not_3_out, not_5_out, nand_4_out);
  nand nand_7 (Q, not_3_out, nand_5_out, Qq);
  nand nand_8 (Qq, Q, nand_6_out, not_4_out);

  // Notes on the sheet:
  //   Flip-Flop JK Mestre-Escravo com Entrada Preset e Clear D
endmodule

module FF_JK_ME_PC_T (
  input  PRESET,
  input  J,
  input  CLK,
  input  CLEAR,
  output Q,
  output Qq
);

  wire nand_1_out, nand_2_out, nand_3_out, nand_4_out, nand_5_out, nand_6_out, not_1_out, not_2_out,
       not_3_out;

  nand nand_1 (nand_1_out, J, CLK, Qq);
  nand nand_2 (nand_2_out, Q, CLK, J);
  not not_1 (not_1_out, PRESET);
  not not_2 (not_2_out, CLEAR);
  nand nand_3 (nand_3_out, not_1_out, nand_1_out, nand_4_out);
  nand nand_4 (nand_4_out, nand_3_out, nand_2_out, not_2_out);
  not not_3 (not_3_out, CLK);
  nand nand_5 (nand_5_out, nand_3_out, not_2_out, not_3_out);
  nand nand_6 (nand_6_out, not_3_out, not_1_out, nand_4_out);
  nand nand_7 (Q, not_1_out, nand_5_out, Qq);
  nand nand_8 (Qq, Q, nand_6_out, not_2_out);

  // Notes on the sheet:
  //   Flip-Flop JK Mestre-Escravo com Entrada Preset e Clear T
endmodule

module SEL (
  input  [3:0] in_1,
  input  in_2,
  output [3:0] out_3
);

  assign out_3 = in_1 & {4{in_2}};  // AND_Gate and_1, 4 bits wide
endmodule

module MUX1 (
  input  E,
  input  SIG,
  output CLR,
  output SET
);

  and and_1 (CLR, ~E, SIG);  // AND_Gate
  and and_2 (SET, E, SIG);
endmodule

module MUX2 (
  input  clk,
  input  key,
  output S2,
  output S1
);

  wire and_1_out, and_2_out, not_1_out, not_2_out;

  and and_1 (and_1_out, ~clk, key);  // AND_Gate
  not not_1 (not_1_out, and_1_out);
  xor xor_1 (S2, not_1_out, not_2_out);
  and and_2 (and_2_out, clk, ~key);  // AND_Gate
  not not_2 (not_2_out, and_2_out);
  xor xor_2 (S1, S2, not_2_out);
endmodule

module decodificador_hex (
  input  [3:0] in_1,
  output [6:0] out_2
);

  wire and_1_out, and_2_out, and_3_out, and_4_out, and_5_out, and_6_out, and_7_out, and_8_out, and_9_out,
       and_10_out, and_11_out, and_12_out, and_13_out, and_14_out, and_15_out, and_16_out, and_17_out,
       and_18_out, and_19_out, and_20_out, and_21_out, and_22_out, and_23_out, and_24_out, and_25_out,
       and_26_out, and_27_out, and_28_out, and_29_out, and_30_out, and_31_out, and_32_out, and_33_out,
       and_34_out, and_35_out, not_1_out, not_2_out, not_3_out, not_4_out;

  not not_1 (not_1_out, in_1[3]);
  not not_2 (not_2_out, in_1[2]);
  not not_3 (not_3_out, in_1[1]);
  not not_4 (not_4_out, in_1[0]);
  and and_1 (and_1_out, not_2_out, not_4_out);
  and and_2 (and_2_out, not_1_out, in_1[1]);
  and and_3 (and_3_out, not_1_out, in_1[2], in_1[0]);
  and and_4 (and_4_out, in_1[3], not_2_out, not_3_out);
  and and_5 (and_5_out, in_1[3], not_4_out);
  and and_6 (and_6_out, in_1[2], in_1[1]);
  and and_7 (and_7_out, not_1_out, not_3_out, not_4_out);
  and and_8 (and_8_out, not_1_out, in_1[1], in_1[0]);
  and and_9 (and_9_out, not_2_out, not_4_out);
  and and_10 (and_10_out, in_1[3], not_3_out, in_1[0]);
  and and_11 (and_11_out, not_1_out, not_2_out);
  and and_12 (and_12_out, not_1_out, in_1[2]);
  and and_13 (and_13_out, in_1[3], not_2_out);
  and and_14 (and_14_out, not_3_out, in_1[0]);
  and and_15 (and_15_out, not_2_out, not_3_out);
  and and_16 (and_16_out, not_2_out, in_1[0]);
  and and_17 (and_17_out, in_1[2], not_3_out, in_1[0]);
  and and_18 (and_18_out, not_1_out, not_2_out, not_4_out);
  and and_19 (and_19_out, not_2_out, in_1[1], in_1[0]);
  and and_20 (and_20_out, in_1[3], not_3_out);
  and and_21 (and_21_out, in_1[2], in_1[1], not_4_out);
  and and_22 (and_22_out, not_2_out, not_4_out);
  and and_23 (and_23_out, in_1[1], not_4_out);
  and and_24 (and_24_out, in_1[3], in_1[1]);
  and and_25 (and_25_out, in_1[3], in_1[2]);
  and and_26 (and_26_out, not_3_out, not_4_out);
  and and_27 (and_27_out, not_1_out, in_1[2], not_3_out);
  and and_28 (and_28_out, in_1[2], not_4_out);
  and and_29 (and_29_out, in_1[3], not_2_out);
  and and_30 (and_30_out, in_1[3], in_1[1]);
  and and_31 (and_31_out, not_2_out, in_1[1]);
  and and_32 (and_32_out, in_1[3], not_2_out);
  and and_33 (and_33_out, not_1_out, in_1[2], not_3_out);
  and and_34 (and_34_out, in_1[1], not_4_out);
  and and_35 (and_35_out, in_1[3], in_1[0]);
  or or_1 (out_2[0], and_1_out, and_2_out, and_3_out, and_4_out, and_5_out, and_6_out);
  or or_2 (out_2[1], and_7_out, and_8_out, and_9_out, and_10_out, and_11_out);
  or or_3 (out_2[2], and_12_out, and_13_out, and_14_out, and_15_out, and_16_out);
  or or_4 (out_2[3], and_17_out, and_18_out, and_19_out, and_20_out, and_21_out);
  or or_5 (out_2[4], and_22_out, and_23_out, and_24_out, and_25_out);
  or or_6 (out_2[5], and_26_out, and_27_out, and_28_out, and_29_out, and_30_out);
  or or_7 (out_2[6], and_31_out, and_32_out, and_33_out, and_34_out, and_35_out);
endmodule

module conhecidencia_vetor (
  input  [3:0] in_1,
  input  [3:0] in_2,
  output out_3
);

  wire and_1_out;
  wire [3:0] not_1_out, xor_1_out;

  assign xor_1_out = in_1 ^ in_2;  // XOR_Gate xor_1, 4 bits wide
  assign not_1_out = ~xor_1_out;  // NOT_Gate not_1, 4 bits wide
  and and_1 (and_1_out, not_1_out[0], not_1_out[1], not_1_out[2], not_1_out[3]);
  not not_2 (out_3, and_1_out);
endmodule

module main_vhdl (
);

  wire not_1_out, not_2_out, not_3_out, not_4_out, not_5_out, not_6_out, not_7_out, not_8_out, not_9_out,
       not_10_out, not_11_out, not_12_out, not_13_out, not_14_out, not_15_out, not_16_out;
  wire [3:0] S;
  wire [6:0] decodificador_hex_1_out_2;

  not not_1 (not_1_out, S[3]);
  not not_2 (not_2_out, S[3]);
  _7_Segment_Display u_7_segment_display_1 (
    .f(not_1_out), .a(not_2_out), .b(1'b1), .e(not_3_out), .d(not_4_out), .c(1'b1));  // open: g, dp
  not not_3 (not_3_out, S[3]);
  not not_4 (not_4_out, S[3]);
  not not_5 (not_5_out, S[2]);
  not not_6 (not_6_out, S[2]);
  not not_7 (not_7_out, S[1]);
  _7_Segment_Display u_7_segment_display_2 (
    .f(not_7_out), .a(not_12_out), .b(1'b1), .e(not_9_out), .d(not_10_out), .c(1'b1));  // open: g, dp
  _7_Segment_Display u_7_segment_display_3 (
    .f(not_5_out), .a(not_6_out), .b(1'b1), .e(not_11_out), .d(not_8_out), .c(1'b1));  // open: g, dp
  not not_8 (not_8_out, S[2]);
  not not_9 (not_9_out, S[1]);
  not not_10 (not_10_out, S[1]);
  not not_11 (not_11_out, S[2]);
  not not_12 (not_12_out, S[1]);
  not not_13 (not_13_out, S[0]);
  not not_14 (not_14_out, S[0]);
  _7_Segment_Display u_7_segment_display_4 (
    .f(not_13_out), .a(not_14_out), .b(1'b1), .e(not_15_out), .d(not_16_out), .c(1'b1));  // open: g, dp
  not not_15 (not_15_out, S[0]);
  not not_16 (not_16_out, S[0]);
  decodificador_hex decodificador_hex_1 (.in_1(S), .out_2(decodificador_hex_1_out_2));
  _7_Segment_Display u_7_segment_display_5 (
    .g(decodificador_hex_1_out_2[6]), .f(decodificador_hex_1_out_2[5]), .a(decodificador_hex_1_out_2[0]),
    .b(decodificador_hex_1_out_2[1]), .e(decodificador_hex_1_out_2[4]), .d(decodificador_hex_1_out_2[3]),
    .c(decodificador_hex_1_out_2[2]));  // open: dp
  contador_com_chave_vhdl contador_com_chave_vhdl_1 ();  // open: clk, clr, enable, vetorN, vetorM, key, count
  contador_de_n_decr_vhdl contador_de_n_decr_vhdl_1 ();  // open: clk, set, T, N, count
  contador_de_decada_decr_vhdl contador_de_decada_decr_vhdl_1 ();  // open: clk, clr, T, count
  contador_de_pulsos_decr_vhdl contador_de_pulsos_decr_vhdl_1 ();  // open: clk, clr, T, count
  contador_de_n_cresc_vhdl contador_de_n_cresc_vhdl_1 ();  // open: clk, clr, T, N, count
  contador_de_decada_cresc_vhdl contador_de_decada_cresc_vhdl_1 ();  // open: clk, clr, T, count
  contador_de_pulsos_cres_vhdl contador_de_pulsos_cres_vhdl_1 ();  // open: clk, clr, T, count

  // Notes on the sheet:
  //   SAIDA PARALELA
  //   SAÍDA
endmodule

// VHDL entity FF_JK_ME_PC_vhdl, as the project stores it:
library IEEE;
use IEEE.STD_LOGIC_1164.ALL;

entity FF_JK_ME_PC_vhdl is
    Port ( preset : in  STD_LOGIC;   
           J      : in  STD_LOGIC;   
           clk    : in  STD_LOGIC;   
           K      : in  STD_LOGIC;   
           Q      : out STD_LOGIC;   
           Ql     : out STD_LOGIC;   
           clear  : in  STD_LOGIC);  
end FF_JK_ME_PC_vhdl;

architecture Behavioral of FF_JK_ME_PC_vhdl is
    signal Q_int_master  : STD_LOGIC := '0';  
    signal Q_int_slave   : STD_LOGIC := '0';  
begin  

    process (preset, clear, clk)
    begin
        if clear = '1' then
            Q_int_master <= '0';  
        elsif preset = '1' then
            Q_int_master <= '1';    
        elsif rising_edge(clk) then
            case (std_logic_vector'(J & K)) is
                when "00" =>  
                    Q_int_master <= Q_int_master;  
                when "01" =>  
                    Q_int_master <= '0';  
                when "10" =>  
                    Q_int_master <= '1';  
                when "11" =>  
                    Q_int_master <= not Q_int_master;  
                when others =>  
                    Q_int_master <= Q_int_master;  
            end case;
        end if;
    end process;

    Q_int_slave <= Q_int_master;
    Q <= Q_int_slave;  
    Ql <= not Q_int_slave;  

end Behavioral;

// VHDL entity FF_JK_ME_PC_D_vhdl, as the project stores it:
library IEEE;
use IEEE.STD_LOGIC_1164.ALL;

entity FF_JK_ME_PC_D_vhdl is
    Port (
	   PRESET : in STD_LOGIC;
        J      : in STD_LOGIC;
        CLK    : in STD_LOGIC;
        CLEAR  : in STD_LOGIC;
        Q      : out STD_LOGIC;
        QN     : out STD_LOGIC
    );
end FF_JK_ME_PC_D_vhdl;

architecture Behavioral of FF_JK_ME_PC_D_vhdl is
    signal master_q : STD_LOGIC := '0'; 
    signal slave_q : STD_LOGIC := '0';
begin

    process(CLK, PRESET, CLEAR)
    begin
        if (CLEAR = '0') then
            master_q <= '0';
        elsif (PRESET = '0') then
            master_q <= '1';
        elsif rising_edge(CLK) then
            if (J = '0') then
                master_q <= '0'; 
            elsif (J = '1') then
                master_q <= '1'; 
            end if;
        end if;
    end process;

 
    process(CLK, PRESET, CLEAR)
    begin
        if (CLEAR = '0') then
            slave_q <= '0';
        elsif (PRESET = '0') then
            slave_q <= '1';
        elsif falling_edge(CLK) then
            slave_q <= master_q; 
        end if;
    end process;


    Q  <= slave_q;
    QN <= NOT slave_q;


end Behavioral;

// VHDL entity FF_JK_ME_PC_T_vhdl, as the project stores it:
library IEEE;
use IEEE.STD_LOGIC_1164.ALL;

entity FF_JK_ME_PC_T_vhdl is
    Port (
	   PRESET : in STD_LOGIC;
        J      : in STD_LOGIC;
        CLK    : in STD_LOGIC;
        CLEAR  : in STD_LOGIC;
        Q      : out STD_LOGIC;
        QN     : out STD_LOGIC
    );
end FF_JK_ME_PC_T_vhdl;

architecture Behavioral of FF_JK_ME_PC_T_vhdl is
    signal master_q : STD_LOGIC := '0'; 
    signal slave_q : STD_LOGIC := '0';
begin

    process(CLK, PRESET, CLEAR)
    begin
        if (CLEAR = '0') then
            master_q <= '0';
        elsif (PRESET = '0') then
            master_q <= '1';
        elsif rising_edge(CLK) then
            if (J = '0') then
                master_q <= master_q; 
            elsif (J = '1') then
                master_q <= NOT master_q; 
            end if;
        end if;
    end process;

 
    process(CLK, PRESET, CLEAR)
    begin
        if (CLEAR = '0') then
            slave_q <= '0';
        elsif (PRESET = '0') then
            slave_q <= '1';
        elsif falling_edge(CLK) then
            slave_q <= master_q; 
        end if;
    end process;


    Q  <= slave_q;
    QN <= NOT slave_q;


end Behavioral;

// VHDL entity decodificador_hex_vhdl, as the project stores it:
library IEEE;
use IEEE.STD_LOGIC_1164.ALL;

entity decodificador_hex_vhdl is
    Port (
        entrada : in STD_LOGIC_VECTOR(3 downto 0);
        saida   : out STD_LOGIC_VECTOR(6 downto 0)
    );
end decodificador_hex_vhdl;

architecture Behavioral of decodificador_hex_vhdl is
begin
    process(entrada)
    begin
        case entrada is
            when "0000" => saida <= "0111111";
            when "0001" => saida <= "0000110";
            when "0010" => saida <= "1011011";
            when "0011" => saida <= "1001111";
            when "0100" => saida <= "1100110";
            when "0101" => saida <= "1101101";
            when "0110" => saida <= "1111101";
            when "0111" => saida <= "0000111";
            when "1000" => saida <= "1111111";
            when "1001" => saida <= "1101111";
            when "1010" => saida <= "1110111";
            when "1011" => saida <= "1111100";
            when "1100" => saida <= "0111001";
            when "1101" => saida <= "1011110";
            when "1110" => saida <= "1111001";
            when "1111" => saida <= "1110001";
            when others => saida <= "0000000";
        end case;
    end process;
end Behavioral;

// VHDL entity contador_de_pulsos_cres_vhdl, as the project stores it:
library IEEE;
use IEEE.STD_LOGIC_1164.ALL;
use IEEE.STD_LOGIC_ARITH.ALL;
use IEEE.STD_LOGIC_UNSIGNED.ALL;

entity contador_de_pulsos_cres_vhdl is
    Port (
        clk     : in  STD_LOGIC;  -- Entrada de clock
        clr     : in  STD_LOGIC;  -- Entrada para limpar (reset)
        T       : in  STD_LOGIC;  -- Entrada para ativar o contador
        count   : out STD_LOGIC_VECTOR(3 downto 0) -- Saída do contador
    );
end contador_de_pulsos_cres_vhdl;

architecture Behavioral of contador_de_pulsos_cres_vhdl is
    signal count_reg : STD_LOGIC_VECTOR(3 downto 0) := "0000"; -- Contador interno
begin
    process(clk, clr)
    begin
        if clr = '1' then  -- Zera o contador quando 'clr' está ativo
            count_reg <= "0000";
        elsif rising_edge(clk) then  -- Incrementa no clock
            if T = '1' then
                if count_reg = "1111" then  -- Verifica se chegou em F (15)
                    count_reg <= "0000";    -- Volta para 0
                else
                    count_reg <= count_reg + 1;
                end if;
            end if;
        end if;
    end process;

    count <= count_reg; -- Atribui o valor do contador à saída
end Behavioral;

// VHDL entity contador_de_decada_cresc_vhdl, as the project stores it:
library IEEE;
use IEEE.STD_LOGIC_1164.ALL;
use IEEE.STD_LOGIC_ARITH.ALL;
use IEEE.STD_LOGIC_UNSIGNED.ALL;

entity contador_de_decada_cresc_vhdl is
    Port (
        clk     : in  STD_LOGIC;  -- Entrada de clock
        clr     : in  STD_LOGIC;  -- Entrada para limpar (reset)
        T       : in  STD_LOGIC;  -- Entrada para ativar o contador
        count   : out STD_LOGIC_VECTOR(3 downto 0) -- Saída do contador
    );
end contador_de_decada_cresc_vhdl;

architecture Behavioral of contador_de_decada_cresc_vhdl is
    signal count_reg : STD_LOGIC_VECTOR(3 downto 0) := "0000"; -- Contador interno inicializado em 0
begin
    process(clk, clr)
    begin
        if clr = '1' then  -- Zera o contador quando 'clr' está ativo
            count_reg <= "0000";  -- Reinicia o contador em 0
        elsif rising_edge(clk) then  -- Incrementa no clock
            if T = '1' then
                if count_reg = "1000" then  -- Verifica se chegou a 8 (1000 em binário)
                    count_reg <= "0000";    -- Volta para 0
                else
                    count_reg <= count_reg + 1; -- Incrementa o contador
                end if;
            end if;
        end if;
    end process;

    count <= count_reg; -- Atribui o valor do contador à saída
end Behavioral;

// VHDL entity contador_de_n_cresc_vhdl, as the project stores it:
library IEEE;
use IEEE.STD_LOGIC_1164.ALL;
use IEEE.STD_LOGIC_ARITH.ALL;
use IEEE.STD_LOGIC_UNSIGNED.ALL;

entity contador_de_n_cresc_vhdl is
    Port (
        clk     : in  STD_LOGIC;  -- Entrada de clock
        clr     : in  STD_LOGIC;  -- Entrada para limpar (reset)
        T       : in  STD_LOGIC;  -- Entrada para ativar o contador
        N       : in  STD_LOGIC_VECTOR(3 downto 0); -- Valor limite (N) da contagem
        count   : out STD_LOGIC_VECTOR(3 downto 0) -- Saída do contador
    );
end contador_de_n_cresc_vhdl;

architecture Behavioral of contador_de_n_cresc_vhdl is
    signal count_reg : STD_LOGIC_VECTOR(3 downto 0) := "0000"; -- Contador interno inicializado em 0
begin
    process(clk, clr)
    begin
        if clr = '1' then  -- Zera o contador quando 'clr' está ativo
            count_reg <= "0000";  -- Reinicia o contador em 0
        elsif rising_edge(clk) then  -- Incrementa no clock
            if T = '1' then
                if count_reg = N - 1 then  -- Verifica se o contador alcançou N-1
                    count_reg <= "0000";    -- Volta para 0
                else
                    count_reg <= count_reg + 1; -- Incrementa o contador
                end if;
            end if;
        end if;
    end process;

    count <= count_reg; -- Atribui o valor do contador à saída
end Behavioral;

// VHDL entity contador_de_pulsos_decr_vhdl, as the project stores it:
library IEEE;
use IEEE.STD_LOGIC_1164.ALL;
use IEEE.STD_LOGIC_ARITH.ALL;
use IEEE.STD_LOGIC_UNSIGNED.ALL;

entity contador_de_pulsos_decr_vhdl is
    Port (
        clk     : in  STD_LOGIC;  -- Entrada de clock
        clr     : in  STD_LOGIC;  -- Entrada para limpar (reset)
        T       : in  STD_LOGIC;  -- Entrada para ativar o contador
        count   : out STD_LOGIC_VECTOR(3 downto 0) -- Saída do contador
    );
end contador_de_pulsos_decr_vhdl;

architecture Behavioral of contador_de_pulsos_decr_vhdl is
    signal count_reg : STD_LOGIC_VECTOR(3 downto 0) := "1111"; -- Contador interno inicializado em F
begin
    process(clk, clr)
    begin
        if clr = '1' then  -- Zera o contador quando 'clr' está ativo
            count_reg <= "1111";  -- Reinicia o contador em F (15)
        elsif rising_edge(clk) then  -- Decrementa no clock
            if T = '1' then
                if count_reg = "0000" then  -- Verifica se chegou a 0
                    count_reg <= "1111";    -- Volta para F
                else
                    count_reg <= count_reg - 1;
                end if;
            end if;
        end if;
    end process;

    count <= count_reg; -- Atribui o valor do contador à saída
end Behavioral;

// VHDL entity contador_de_decada_decr_vhdl, as the project stores it:
library IEEE;
use IEEE.STD_LOGIC_1164.ALL;
use IEEE.STD_LOGIC_ARITH.ALL;
use IEEE.STD_LOGIC_UNSIGNED.ALL;

entity contador_de_decada_decr_vhdl is
    Port (
        clk     : in  STD_LOGIC;  -- Entrada de clock
        clr     : in  STD_LOGIC;  -- Entrada para limpar (reset)
        T       : in  STD_LOGIC;  -- Entrada para ativar o contador
        count   : out STD_LOGIC_VECTOR(3 downto 0) -- Saída do contador
    );
end contador_de_decada_decr_vhdl;

architecture Behavioral of contador_de_decada_decr_vhdl is
    signal count_reg : STD_LOGIC_VECTOR(3 downto 0) := "1001"; -- Inicializado em 9
begin
    process(clk, clr)
    begin
        if clr = '1' then  -- Zera o contador quando 'clr' está ativo
            count_reg <= "1001";  -- Reinicia o contador em 9
        elsif rising_edge(clk) then  -- Decrementa no clock
            if T = '1' then
                if count_reg = "0001" then  -- Verifica se chegou a 1 (0001 em binário)
                    count_reg <= "1001";    -- Volta para 9
                else
                    count_reg <= count_reg - 1; -- Decrementa o contador
                end if;
            end if;
        end if;
    end process;

    count <= count_reg; -- Atribui o valor do contador à saída
end Behavioral;

// VHDL entity contador_de_n_decr_vhdl, as the project stores it:
library IEEE;
use IEEE.STD_LOGIC_1164.ALL;
use IEEE.STD_LOGIC_ARITH.ALL;
use IEEE.STD_LOGIC_UNSIGNED.ALL;

entity contador_de_n_decr_vhdl is
    Port (
        clk     : in  STD_LOGIC;  -- Entrada de clock
        set     : in  STD_LOGIC;  -- Entrada para ajustar o contador para o valor de N
        T       : in  STD_LOGIC;  -- Entrada para ativar o contador
        N       : in  STD_LOGIC_VECTOR(3 downto 0); -- Valor inicial da contagem (N)
        count   : out STD_LOGIC_VECTOR(3 downto 0) -- Saída do contador
    );
end contador_de_n_decr_vhdl;

architecture Behavioral of contador_de_n_decr_vhdl is
    signal count_reg : STD_LOGIC_VECTOR(3 downto 0) := "0000"; -- Contador interno
begin
    process(clk, set)
    begin
        if set = '1' then  -- Ajusta o contador para o valor de N quando 'set' está ativo
            count_reg <= N; -- Contador recebe o valor de N
        elsif rising_edge(clk) then
            if T = '1' then
                if N = "0000" then  -- Se N for 0000, a saída permanece 0000
                    count_reg <= "0000";
                elsif count_reg = "0001" then  -- Verifica se o contador alcançou 1
                    count_reg <= N;           -- Retorna para N
                else
                    count_reg <= count_reg - 1; -- Decrementa o contador
                end if;
            end if;
        end if;
    end process;

    count <= count_reg; -- Atribui o valor do contador à saída
end Behavioral;

// VHDL entity contador_com_chave_vhdl, as the project stores it:
library IEEE;
use IEEE.STD_LOGIC_1164.ALL;
use IEEE.NUMERIC_STD.ALL;  -- Usando a biblioteca numeric_std para conversão de tipos

entity contador_com_chave_vhdl is
    Port (
        clk     : in  STD_LOGIC;              -- Entrada de clock
        clr     : in  STD_LOGIC;              -- Entrada de clear (reset)
        enable  : in  STD_LOGIC;              -- Entrada de enable para ativar a contagem
        vetorN  : in  STD_LOGIC_VECTOR(3 downto 0); -- Valor inicial da contagem (vetorN)
        vetorM  : in  STD_LOGIC_VECTOR(3 downto 0); -- Valor final da contagem (vetorM)
        key     : in  STD_LOGIC;              -- Chave para inverter a contagem (0 - crescente, 1 - decrescente)
        count   : out STD_LOGIC_VECTOR(3 downto 0) -- Saída do contador
    );
end contador_com_chave_vhdl;

architecture Behavioral of contador_com_chave_vhdl is
    signal count_reg : STD_LOGIC_VECTOR(3 downto 0) := "0000"; -- Contador interno
    signal N_int, M_int : integer range 0 to 15; -- Variáveis internas para armazenar os valores de N e M como inteiros
begin
    -- Convertendo os valores de vetorN e vetorM de STD_LOGIC_VECTOR para inteiros
    N_int <= to_integer(unsigned(vetorN));
    M_int <= to_integer(unsigned(vetorM));

    process(clk, clr)
    begin
        if clr = '1' then  -- Ajusta o contador para o valor de N quando 'clr' está ativo
            count_reg <= vetorN; -- Contador recebe o valor de vetorN
        elsif rising_edge(clk) then
            if enable = '1' then  -- O contador só incrementa ou decrementa quando enable está ativo
                if key = '0' then  -- Contagem crescente de N até M-1
                    if to_integer(unsigned(count_reg)) = M_int - 1 then
                        count_reg <= vetorN;  -- Quando atingir M-1, volta para N
                    else
                        count_reg <= std_logic_vector(to_unsigned(to_integer(unsigned(count_reg)) + 1, 4)); -- Incrementa o contador
                    end if;
                elsif key = '1' then  -- Contagem decrescente de M até N+1
                    if to_integer(unsigned(count_reg)) = N_int + 1 then
                        count_reg <= vetorM;  -- Quando atingir N+1, volta para M
                    else
                        count_reg <= std_logic_vector(to_unsigned(to_integer(unsigned(count_reg)) - 1, 4)); -- Decrementa o contador
                    end if;
                end if;
            end if;
        end if;
    end process;

    count <= count_reg; -- Atribui o valor do contador à saída
end Behavioral;
